// Logisim project G06_th1_combinational.circ as structural Verilog: 23 circuits, main circuit main
module main (
  input  [15:0] A,
  input  SUB,
  input  [15:0] B,
  input  [4:0] SH,
  output [15:0] S,
  output COUT,
  output OVF,
  output [15:0] Y_shl,
  output [15:0] Y_shr,
  output GT,
  output EQ,
  output LT
);

  addsub16 addsub16_1 (.A(A), .B(B), .SUB(SUB), .S(S), .COUT(COUT), .OVF(OVF));
  shl16 shl16_1 (.A_16(A), .SHL_5(SH), .Y_16(Y_shl));
  shr16 shr16_1 (.A(A), .SHR_5(SH), .Y_16(Y_shr));
  cmp16 cmp16_1 (.A(A), .B(B), .GT(GT), .EQ(EQ), .LT(LT));
endmodule

module half_adder (
  input  A,
  input  B,
  output SUM,
  output COUT
);

  xor xor_1 (SUM, A, B);
  and and_1 (COUT, B, A);
endmodule

module full_adder (
  input  A,
  input  B,
  input  CIN,
  output COUT,
  output SUM
);

  wire half_adder_1_cout, half_adder_1_sum, half_adder_2_cout;

  half_adder half_adder_1 (.A(A), .B(B), .SUM(half_adder_1_sum), .COUT(half_adder_1_cout));
  half_adder half_adder_2 (.A(half_adder_1_sum), .B(CIN), .SUM(SUM), .COUT(half_adder_2_cout));
  or or_1 (COUT, half_adder_1_cout, half_adder_2_cout);
endmodule

module adder4 (
  input  CIN,
  input  [3:0] A,
  input  [3:0] B,
  output [3:0] SUM,
  output COUT,
  output LAST_CIN
);

  wire full_adder_1_cout, full_adder_2_cout;

  full_adder full_adder_1 (.A(A[0]), .B(B[0]), .CIN(CIN), .COUT(full_adder_1_cout), .SUM(SUM[0]));
  full_adder full_adder_2 (.A(A[1]), .B(B[1]), .CIN(full_adder_1_cout), .COUT(full_adder_2_cout), .SUM(SUM[1]));
  full_adder full_adder_3 (.A(A[2]), .B(B[2]), .CIN(full_adder_2_cout), .COUT(LAST_CIN), .SUM(SUM[2]));
  full_adder full_adder_4 (.A(A[3]), .B(B[3]), .CIN(LAST_CIN), .COUT(COUT), .SUM(SUM[3]));
endmodule

module adder16 (
  input  CIN,
  input  [15:0] A,
  input  [15:0] B,
  output [15:0] S,
  output COUT,
  output LAST_CIN
);

  wire adder4_1_cout, adder4_2_cout, adder4_3_cout;

  adder4 adder4_1 (.CIN(CIN), .A(A[3:0]), .B(B[3:0]), .SUM(S[3:0]), .COUT(adder4_1_cout));  // open: LAST_CIN
  adder4 adder4_2 (.CIN(adder4_1_cout), .A(A[7:4]), .B(B[7:4]), .SUM(S[7:4]), .COUT(adder4_2_cout));  // open: LAST_CIN
  adder4 adder4_3 (
    .CIN(adder4_2_cout), .A(A[11:8]), .B(B[11:8]), .SUM(S[11:8]), .COUT(adder4_3_cout));  // open: LAST_CIN
  adder4 adder4_4 (.CIN(adder4_3_cout), .A(A[15:12]), .B(B[15:12]), .SUM(S[15:12]), .COUT(COUT), .LAST_CIN(LAST_CIN));
endmodule

module xor4_helper (
  input  [3:0] A,
  input  CIN,
  output [3:0] XOR_A
);

  xor xor_1 (XOR_A[0], A[0], CIN);
  xor xor_2 (XOR_A[1], A[1], CIN);
  xor xor_3 (XOR_A[2], A[2], CIN);
  xor xor_4 (XOR_A[3], A[3], CIN);
endmodule

module xor16_helper (
  input  [15:0] A,
  input  CIN,
  output [15:0] XOR_A
);

  xor4_helper xor4_helper_1 (.A(A[3:0]), .CIN(CIN), .XOR_A(XOR_A[3:0]));
  xor4_helper xor4_helper_2 (.A(A[7:4]), .CIN(CIN), .XOR_A(XOR_A[7:4]));
  xor4_helper xor4_helper_3 (.A(A[11:8]), .CIN(CIN), .XOR_A(XOR_A[11:8]));
  xor4_helper xor4_helper_4 (.A(A[15:12]), .CIN(CIN), .XOR_A(XOR_A[15:12]));
endmodule

module addsub16 (
  input  [15:0] A,
  input  [15:0] B,
  input  SUB,
  output [15:0] S,
  output COUT,
  output OVF
);

  wire adder16_1_last_cin;
  wire [15:0] xor16_helper_1_xor_a;

  xor16_helper xor16_helper_1 (.A(B), .CIN(SUB), .XOR_A(xor16_helper_1_xor_a));
  adder16 adder16_1 (.CIN(SUB), .A(A), .B(xor16_helper_1_xor_a), .S(S), .COUT(COUT), .LAST_CIN(adder16_1_last_cin));
  xor xor_1 (OVF, COUT, adder16_1_last_cin);
endmodule

module shl8_helper (
  input  [15:0] A,
  output [15:0] Y
);


  assign Y = {A[7:0], {8{1'b0}}};

  // Notes on the sheet:
  //   CONST_0
endmodule

module shl4_helper (
  input  [15:0] A,
  output [15:0] Y
);


  assign Y = {A[11:0], 4'b0000};

  // Notes on the sheet:
  //   CONST_0
endmodule

module shl2_helper (
  input  [15:0] A,
  output [15:0] Y
);


  assign Y = {A[13:0], 2'b00};

  // Notes on the sheet:
  //   CONST_0
endmodule

module shl1_helper (
  input  [15:0] A,
  output [15:0] Y
);


  assign Y = {A[14:0], 1'b0};

  // Notes on the sheet:
  //   CONST_0
endmodule

module shl16 (
  input  [15:0] A_16,
  input  [4:0] SHL_5,
  output [15:0] Y_16
);

  wire [15:0] multiplexer_1_out, multiplexer_2_out, multiplexer_3_out, multiplexer_4_out, shl1_helper_1_y,
       shl2_helper_1_y, shl4_helper_1_y, shl8_helper_1_y, shl_max_helper_1_y;

  shl1_helper shl1_helper_1 (.A(A_16), .Y(shl1_helper_1_y));
  Multiplexer #(.width(16)) multiplexer_1 (.in0(A_16), .in1(shl1_helper_1_y), .out(multiplexer_1_out), .sel(SHL_5[0]));
  shl2_helper shl2_helper_1 (.A(multiplexer_1_out), .Y(shl2_helper_1_y));
  Multiplexer #(.width(16)) multiplexer_2 (
    .in0(multiplexer_1_out), .in1(shl2_helper_1_y), .out(multiplexer_2_out), .sel(SHL_5[1]));
  shl4_helper shl4_helper_1 (.A(multiplexer_2_out), .Y(shl4_helper_1_y));
  Multiplexer #(.width(16)) multiplexer_3 (
    .in0(multiplexer_2_out), .in1(shl4_helper_1_y), .out(multiplexer_3_out), .sel(SHL_5[2]));
  shl8_helper shl8_helper_1 (.A(multiplexer_3_out), .Y(shl8_helper_1_y));
  Multiplexer #(.width(16)) multiplexer_4 (
    .in0(multiplexer_3_out), .in1(shl8_helper_1_y), .out(multiplexer_4_out), .sel(SHL_5[3]));
  shl_max_helper shl_max_helper_1 (.A(multiplexer_4_out), .Y(shl_max_helper_1_y));
  Multiplexer #(.width(16)) multiplexer_5 (
    .in0(multiplexer_4_out), .in1(shl_max_helper_1_y), .out(Y_16), .sel(SHL_5[4]));
endmodule

module shr8_helper (
  input  [15:0] A,
  output [15:0] Y
);


  assign Y = {{8{1'b0}}, A[15:8]};

  // Notes on the sheet:
  //   CONST_0
endmodule

module shr4_helper (
  input  [15:0] A,
  output [15:0] Y
);


  assign Y = {4'b0000, A[15:4]};

  // Notes on the sheet:
  //   CONST_0
endmodule

module shr2_helper (
  input  [15:0] A,
  output [15:0] Y
);


  assign Y = {2'b00, A[15:2]};

  // Notes on the sheet:
  //   CONST_0
endmodule

module shr1_helper (
  input  [15:0] A,
  output [15:0] Y
);


  assign Y = {1'b0, A[15:1]};

  // Notes on the sheet:
  //   CONST_0
endmodule

module shr16 (
  input  [15:0] A,
  input  [4:0] SHR_5,
  output [15:0] Y_16
);

  wire [15:0] multiplexer_1_out, multiplexer_2_out, multiplexer_3_out, multiplexer_4_out, shr1_helper_1_y,
       shr2_helper_1_y, shr4_helper_1_y, shr8_helper_1_y, shr_max_helper_1_y;

  shr1_helper shr1_helper_1 (.A(A), .Y(shr1_helper_1_y));
  Multiplexer #(.width(16)) multiplexer_1 (.in0(A), .in1(shr1_helper_1_y), .out(multiplexer_1_out), .sel(SHR_5[0]));
  shr2_helper shr2_helper_1 (.A(multiplexer_1_out), .Y(shr2_helper_1_y));
  Multiplexer #(.width(16)) multiplexer_2 (
    .in0(multiplexer_1_out), .in1(shr2_helper_1_y), .out(multiplexer_2_out), .sel(SHR_5[1]));
  shr4_helper shr4_helper_1 (.A(multiplexer_2_out), .Y(shr4_helper_1_y));
  Multiplexer #(.width(16)) multiplexer_3 (
    .in0(multiplexer_2_out), .in1(shr4_helper_1_y), .out(multiplexer_3_out), .sel(SHR_5[2]));
  shr8_helper shr8_helper_1 (.A(multiplexer_3_out), .Y(shr8_helper_1_y));
  Multiplexer #(.width(16)) multiplexer_4 (
    .in0(multiplexer_3_out), .in1(shr8_helper_1_y), .out(multiplexer_4_out), .sel(SHR_5[3]));
  shr_max_helper shr_max_helper_1 (.A(multiplexer_4_out), .Y(shr_max_helper_1_y));
  Multiplexer #(.width(16)) multiplexer_5 (
    .in0(multiplexer_4_out), .in1(shr_max_helper_1_y), .out(Y_16), .sel(SHR_5[4]));
endmodule

module shl_max_helper (
  input  [15:0] A,
  output [15:0] Y
);

  assign Y = A & {16{1'b0}};  // AND_Gate and_1, 16 bits wide

  // Notes on the sheet:
  //   CONST_0
endmodule

module shr_max_helper (
  input  [15:0] A,
  output [15:0] Y
);

  assign Y = A & {16{1'b0}};  // AND_Gate and_1, 16 bits wide

  // Notes on the sheet:
  //   CONST_0
endmodule

module one_bit_comp_helper (
  input  A,
  input  B,
  input  GTin,
  input  EQin,
  input  LTin,
  output GT,
  output EQ,
  output LT
);

  wire demultiplexer_1_out1, demultiplexer_2_out0, demultiplexer_2_out1, xor_1_out;

  Demultiplexer demultiplexer_1 (.out0(EQ), .out1(demultiplexer_1_out1), .in(EQin), .sel(xor_1_out));
  xor xor_1 (xor_1_out, A, B);
  Demultiplexer demultiplexer_2 (
    .out0(demultiplexer_2_out0), .out1(demultiplexer_2_out1), .in(demultiplexer_1_out1), .sel(B));
  Multiplexer multiplexer_1 (.in0(demultiplexer_2_out0), .in1(GTin), .out(GT), .sel(GTin));
  Multiplexer multiplexer_2 (.in0(demultiplexer_2_out1), .in1(LTin), .out(LT), .sel(LTin));
endmodule

module cmp4 (
  input  [3:0] A,
  input  [3:0] B,
  input  GTin,
  input  EQin,
  input  LTin,
  output GT,
  output EQ,
  output LT
);

  wire one_bit_comp_helper_1_eq, one_bit_comp_helper_1_gt, one_bit_comp_helper_1_lt,
       one_bit_comp_helper_2_eq, one_bit_comp_helper_2_gt, one_bit_comp_helper_2_lt,
       one_bit_comp_helper_3_eq, one_bit_comp_helper_3_gt, one_bit_comp_helper_3_lt;

  one_bit_comp_helper one_bit_comp_helper_1 (
    .A(A[3]), .B(B[3]), .GTin(GTin), .EQin(EQin), .LTin(LTin), .GT(one_bit_comp_helper_1_gt),
    .EQ(one_bit_comp_helper_1_eq), .LT(one_bit_comp_helper_1_lt));
  one_bit_comp_helper one_bit_comp_helper_2 (
    .A(A[2]), .B(B[2]), .GTin(one_bit_comp_helper_1_gt), .EQin(one_bit_comp_helper_1_eq),
    .LTin(one_bit_comp_helper_1_lt), .GT(one_bit_comp_helper_2_gt), .EQ(one_bit_comp_helper_2_eq),
    .LT(one_bit_comp_helper_2_lt));
  one_bit_comp_helper one_bit_comp_helper_3 (
    .A(A[1]), .B(B[1]), .GTin(one_bit_comp_helper_2_gt), .EQin(one_bit_comp_helper_2_eq),
    .LTin(one_bit_comp_helper_2_lt), .GT(one_bit_comp_helper_3_gt), .EQ(one_bit_comp_helper_3_eq),
    .LT(one_bit_comp_helper_3_lt));
  one_bit_comp_helper one_bit_comp_helper_4 (
    .A(A[0]), .B(B[0]), .GTin(one_bit_comp_helper_3_gt), .EQin(one_bit_comp_helper_3_eq),
    .LTin(one_bit_comp_helper_3_lt), .GT(GT), .EQ(EQ), .LT(LT));
endmodule

module cmp16 (
  input  [15:0] A,
  input  [15:0] B,
  output GT,
  output EQ,
  output LT
);

  wire cmp4_1_eq, cmp4_1_gt, cmp4_1_lt, cmp4_2_eq, cmp4_2_gt, cmp4_2_lt, cmp4_3_eq, cmp4_3_gt, cmp4_3_lt,
       not_1_out, not_2_out, one_bit_comp_helper_1_eq, one_bit_comp_helper_1_gt, one_bit_comp_helper_1_lt;

  cmp4 cmp4_1 (
    .A(A[15:12]), .B(B[15:12]), .GTin(one_bit_comp_helper_1_gt), .EQin(one_bit_comp_helper_1_eq),
    .LTin(one_bit_comp_helper_1_lt), .GT(cmp4_1_gt), .EQ(cmp4_1_eq), .LT(cmp4_1_lt));
  not not_1 (not_1_out, A[15]);
  not not_2 (not_2_out, B[15]);
  cmp4 cmp4_2 (
    .A(A[11:8]), .B(B[11:8]), .GTin(cmp4_1_gt), .EQin(cmp4_1_eq), .LTin(cmp4_1_lt), .GT(cmp4_2_gt),
    .EQ(cmp4_2_eq), .LT(cmp4_2_lt));
  one_bit_comp_helper one_bit_comp_helper_1 (
    .A(not_1_out), .B(not_2_out), .GTin(1'b0), .EQin(1'b1), .LTin(1'b0), .GT(one_bit_comp_helper_1_gt),
    .EQ(one_bit_comp_helper_1_eq), .LT(one_bit_comp_helper_1_lt));
  cmp4 cmp4_3 (
    .A(A[7:4]), .B(B[7:4]), .GTin(cmp4_2_gt), .EQin(cmp4_2_eq), .LTin(cmp4_2_lt), .GT(cmp4_3_gt),
    .EQ(cmp4_3_eq), .LT(cmp4_3_lt));
  cmp4 cmp4_4 (.A(A[3:0]), .B(B[3:0]), .GTin(cmp4_3_gt), .EQin(cmp4_3_eq), .LTin(cmp4_3_lt), .GT(GT), .EQ(EQ), .LT(LT));
endmodule
