// Logisim project G06_th2_alu.circ as structural Verilog: 25 circuits, main circuit main_CS25B018_CS25B095
module main_CS25B018_CS25B095 (
  input  [4:0] OPCODE,
  input  [15:0] A,
  input  [15:0] B,
  input  ALU_OP,
  output Z,
  output N,
  output C,
  output V,
  output [15:0] BUS_OUT
);

  alu_CS25B018_CS25B095 alu_cs25b018_cs25b095_1 (
    .OPCODE(OPCODE), .A(A), .B(B), .ALU_OUTPUT_ENABLE(ALU_OP), .Z(Z), .N(N), .C(C), .V(V), .BUS_OUT(BUS_OUT));
endmodule

module half_adder_CS25B018_CS25B095 (
  input  A,
  input  B,
  output SUM,
  output COUT
);

  xor xor_1 (SUM, A, B);
  and and_1 (COUT, B, A);
endmodule

module full_adder_CS25B018_CS25B095 (
  input  A,
  input  B,
  input  CIN,
  output COUT,
  output SUM
);

  wire half_adder_cs25b018_cs25b095_1_cout, half_adder_cs25b018_cs25b095_1_sum,
       half_adder_cs25b018_cs25b095_2_cout;

  half_adder_CS25B018_CS25B095 half_adder_cs25b018_cs25b095_1 (
    .A(A), .B(B), .SUM(half_adder_cs25b018_cs25b095_1_sum), .COUT(half_adder_cs25b018_cs25b095_1_cout));
  half_adder_CS25B018_CS25B095 half_adder_cs25b018_cs25b095_2 (
    .A(half_adder_cs25b018_cs25b095_1_sum), .B(CIN), .SUM(SUM), .COUT(half_adder_cs25b018_cs25b095_2_cout));
  or or_1 (COUT, half_adder_cs25b018_cs25b095_1_cout, half_adder_cs25b018_cs25b095_2_cout);
endmodule

module adder4_CS25B018_CS25B095 (
  input  CIN,
  input  [3:0] A,
  input  [3:0] B,
  output [3:0] SUM,
  output COUT,
  output LAST_CIN
);

  wire full_adder_cs25b018_cs25b095_1_cout, full_adder_cs25b018_cs25b095_2_cout;

  full_adder_CS25B018_CS25B095 full_adder_cs25b018_cs25b095_1 (
    .A(A[0]), .B(B[0]), .CIN(CIN), .COUT(full_adder_cs25b018_cs25b095_1_cout), .SUM(SUM[0]));
  full_adder_CS25B018_CS25B095 full_adder_cs25b018_cs25b095_2 (
    .A(A[1]), .B(B[1]), .CIN(full_adder_cs25b018_cs25b095_1_cout),
    .COUT(full_adder_cs25b018_cs25b095_2_cout), .SUM(SUM[1]));
  full_adder_CS25B018_CS25B095 full_adder_cs25b018_cs25b095_3 (
    .A(A[2]), .B(B[2]), .CIN(full_adder_cs25b018_cs25b095_2_cout), .COUT(LAST_CIN), .SUM(SUM[2]));
  full_adder_CS25B018_CS25B095 full_adder_cs25b018_cs25b095_4 (
    .A(A[3]), .B(B[3]), .CIN(LAST_CIN), .COUT(COUT), .SUM(SUM[3]));
endmodule

module adder16_CS25B018_CS25B095 (
  input  CIN,
  input  [15:0] A,
  input  [15:0] B,
  output [15:0] S,
  output COUT,
  output LAST_CIN
);

  wire adder4_cs25b018_cs25b095_1_cout, adder4_cs25b018_cs25b095_2_cout, adder4_cs25b018_cs25b095_3_cout;

  adder4_CS25B018_CS25B095 adder4_cs25b018_cs25b095_1 (
    .CIN(CIN), .A(A[3:0]), .B(B[3:0]), .SUM(S[3:0]), .COUT(adder4_cs25b018_cs25b095_1_cout));  // open: LAST_CIN
  adder4_CS25B018_CS25B095 adder4_cs25b018_cs25b095_2 (
    .CIN(adder4_cs25b018_cs25b095_1_cout), .A(A[7:4]), .B(B[7:4]), .SUM(S[7:4]),
    .COUT(adder4_cs25b018_cs25b095_2_cout));  // open: LAST_CIN
  adder4_CS25B018_CS25B095 adder4_cs25b018_cs25b095_3 (
    .CIN(adder4_cs25b018_cs25b095_2_cout), .A(A[11:8]), .B(B[11:8]), .SUM(S[11:8]),
    .COUT(adder4_cs25b018_cs25b095_3_cout));  // open: LAST_CIN
  adder4_CS25B018_CS25B095 adder4_cs25b018_cs25b095_4 (
    .CIN(adder4_cs25b018_cs25b095_3_cout), .A(A[15:12]), .B(B[15:12]), .SUM(S[15:12]), .COUT(COUT),
    .LAST_CIN(LAST_CIN));
endmodule

module xor4_helper_CS25B018_CS25B095 (
  input  [3:0] A,
  input  CIN,
  output [3:0] XOR_A
);

  xor xor_1 (XOR_A[0], A[0], CIN);
  xor xor_2 (XOR_A[1], A[1], CIN);
  xor xor_3 (XOR_A[2], A[2], CIN);
  xor xor_4 (XOR_A[3], A[3], CIN);
endmodule

module xor16_helper_CS25B018_CS25B095 (
  input  [15:0] A,
  input  CIN,
  output [15:0] XOR_A
);

  xor4_helper_CS25B018_CS25B095 xor4_helper_cs25b018_cs25b095_1 (.A(A[3:0]), .CIN(CIN), .XOR_A(XOR_A[3:0]));
  xor4_helper_CS25B018_CS25B095 xor4_helper_cs25b018_cs25b095_2 (.A(A[7:4]), .CIN(CIN), .XOR_A(XOR_A[7:4]));
  xor4_helper_CS25B018_CS25B095 xor4_helper_cs25b018_cs25b095_3 (.A(A[11:8]), .CIN(CIN), .XOR_A(XOR_A[11:8]));
  xor4_helper_CS25B018_CS25B095 xor4_helper_cs25b018_cs25b095_4 (.A(A[15:12]), .CIN(CIN), .XOR_A(XOR_A[15:12]));
endmodule

module addsub16_CS25B018_CS25B095 (
  input  [15:0] A,
  input  [15:0] B,
  input  SUB,
  output [15:0] S,
  output COUT,
  output OVF
);

  wire adder16_cs25b018_cs25b095_1_last_cin;
  wire [15:0] xor16_helper_cs25b018_cs25b095_1_xor_a;

  xor16_helper_CS25B018_CS25B095 xor16_helper_cs25b018_cs25b095_1 (
    .A(B), .CIN(SUB), .XOR_A(xor16_helper_cs25b018_cs25b095_1_xor_a));
  adder16_CS25B018_CS25B095 adder16_cs25b018_cs25b095_1 (
    .CIN(SUB), .A(A), .B(xor16_helper_cs25b018_cs25b095_1_xor_a), .S(S), .COUT(COUT),
    .LAST_CIN(adder16_cs25b018_cs25b095_1_last_cin));
  xor xor_1 (OVF, COUT, adder16_cs25b018_cs25b095_1_last_cin);
endmodule

module shl8_helper_CS25B018_CS25B095 (
  input  [15:0] A,
  output [15:0] Y
);


  assign Y = {A[7:0], {8{1'b0}}};

  // Notes on the sheet:
  //   CONST_0
endmodule

module shl4_helper_CS25B018_CS25B095 (
  input  [15:0] A,
  output [15:0] Y
);


  assign Y = {A[11:0], 4'b0000};

  // Notes on the sheet:
  //   CONST_0
endmodule

module shl2_helper_CS25B018_CS25B095 (
  input  [15:0] A,
  output [15:0] Y
);


  assign Y = {A[13:0], 2'b00};

  // Notes on the sheet:
  //   CONST_0
endmodule

module shl1_helper_CS25B018_CS25B095 (
  input  [15:0] A,
  output [15:0] Y
);


  assign Y = {A[14:0], 1'b0};

  // Notes on the sheet:
  //   CONST_0
endmodule

module shl16_CS25B018_CS25B095 (
  input  [15:0] A,
  input  [4:0] SHL_5,
  output [15:0] Y_16
);

  wire [15:0] multiplexer_1_out, multiplexer_2_out, multiplexer_3_out, multiplexer_4_out,
       shl1_helper_cs25b018_cs25b095_1_y, shl2_helper_cs25b018_cs25b095_1_y,
       shl4_helper_cs25b018_cs25b095_1_y, shl8_helper_cs25b018_cs25b095_1_y,
       shl_max_helper_cs25b018_cs25b095_1_y;

  shl1_helper_CS25B018_CS25B095 shl1_helper_cs25b018_cs25b095_1 (.A(A), .Y(shl1_helper_cs25b018_cs25b095_1_y));
  Multiplexer #(.width(16)) multiplexer_1 (
    .in0(A), .in1(shl1_helper_cs25b018_cs25b095_1_y), .out(multiplexer_1_out), .sel(SHL_5[0]));
  shl2_helper_CS25B018_CS25B095 shl2_helper_cs25b018_cs25b095_1 (
    .A(multiplexer_1_out), .Y(shl2_helper_cs25b018_cs25b095_1_y));
  Multiplexer #(.width(16)) multiplexer_2 (
    .in0(multiplexer_1_out), .in1(shl2_helper_cs25b018_cs25b095_1_y), .out(multiplexer_2_out), .sel(SHL_5[1]));
  shl4_helper_CS25B018_CS25B095 shl4_helper_cs25b018_cs25b095_1 (
    .A(multiplexer_2_out), .Y(shl4_helper_cs25b018_cs25b095_1_y));
  Multiplexer #(.width(16)) multiplexer_3 (
    .in0(multiplexer_2_out), .in1(shl4_helper_cs25b018_cs25b095_1_y), .out(multiplexer_3_out), .sel(SHL_5[2]));
  shl8_helper_CS25B018_CS25B095 shl8_helper_cs25b018_cs25b095_1 (
    .A(multiplexer_3_out), .Y(shl8_helper_cs25b018_cs25b095_1_y));
  Multiplexer #(.width(16)) multiplexer_4 (
    .in0(multiplexer_3_out), .in1(shl8_helper_cs25b018_cs25b095_1_y), .out(multiplexer_4_out), .sel(SHL_5[3]));
  shl_max_helper_CS25B018_CS25B095 shl_max_helper_cs25b018_cs25b095_1 (
    .A(multiplexer_4_out), .Y(shl_max_helper_cs25b018_cs25b095_1_y));
  Multiplexer #(.width(16)) multiplexer_5 (
    .in0(multiplexer_4_out), .in1(shl_max_helper_cs25b018_cs25b095_1_y), .out(Y_16), .sel(SHL_5[4]));
endmodule

module shr8_helper_CS25B018_CS25B095 (
  input  [15:0] A,
  output [15:0] Y
);


  assign Y = {{8{1'b0}}, A[15:8]};

  // Notes on the sheet:
  //   CONST_0
endmodule

module shr4_helper_CS25B018_CS25B095 (
  input  [15:0] A,
  output [15:0] Y
);


  assign Y = {4'b0000, A[15:4]};

  // Notes on the sheet:
  //   CONST_0
endmodule

module shr2_helper_CS25B018_CS25B095 (
  input  [15:0] A,
  output [15:0] Y
);


  assign Y = {2'b00, A[15:2]};

  // Notes on the sheet:
  //   CONST_0
endmodule

module shr1_helper_CS25B018_CS25B095 (
  input  [15:0] A,
  output [15:0] Y
);


  assign Y = {1'b0, A[15:1]};

  // Notes on the sheet:
  //   CONST_0
endmodule

module shr16_CS25B018_CS25B095 (
  input  [15:0] A,
  input  [4:0] SHR_5,
  output [15:0] Y_16
);

  wire [15:0] multiplexer_1_out, multiplexer_2_out, multiplexer_3_out, multiplexer_4_out,
       shr1_helper_cs25b018_cs25b095_1_y, shr2_helper_cs25b018_cs25b095_1_y,
       shr4_helper_cs25b018_cs25b095_1_y, shr8_helper_cs25b018_cs25b095_1_y,
       shr_max_helper_cs25b018_cs25b095_1_y;

  shr1_helper_CS25B018_CS25B095 shr1_helper_cs25b018_cs25b095_1 (.A(A), .Y(shr1_helper_cs25b018_cs25b095_1_y));
  Multiplexer #(.width(16)) multiplexer_1 (
    .in0(A), .in1(shr1_helper_cs25b018_cs25b095_1_y), .out(multiplexer_1_out), .sel(SHR_5[0]));
  shr2_helper_CS25B018_CS25B095 shr2_helper_cs25b018_cs25b095_1 (
    .A(multiplexer_1_out), .Y(shr2_helper_cs25b018_cs25b095_1_y));
  Multiplexer #(.width(16)) multiplexer_2 (
    .in0(multiplexer_1_out), .in1(shr2_helper_cs25b018_cs25b095_1_y), .out(multiplexer_2_out), .sel(SHR_5[1]));
  shr4_helper_CS25B018_CS25B095 shr4_helper_cs25b018_cs25b095_1 (
    .A(multiplexer_2_out), .Y(shr4_helper_cs25b018_cs25b095_1_y));
  Multiplexer #(.width(16)) multiplexer_3 (
    .in0(multiplexer_2_out), .in1(shr4_helper_cs25b018_cs25b095_1_y), .out(multiplexer_3_out), .sel(SHR_5[2]));
  shr8_helper_CS25B018_CS25B095 shr8_helper_cs25b018_cs25b095_1 (
    .A(multiplexer_3_out), .Y(shr8_helper_cs25b018_cs25b095_1_y));
  Multiplexer #(.width(16)) multiplexer_4 (
    .in0(multiplexer_3_out), .in1(shr8_helper_cs25b018_cs25b095_1_y), .out(multiplexer_4_out), .sel(SHR_5[3]));
  shr_max_helper_CS25B018_CS25B095 shr_max_helper_cs25b018_cs25b095_1 (
    .A(multiplexer_4_out), .Y(shr_max_helper_cs25b018_cs25b095_1_y));
  Multiplexer #(.width(16)) multiplexer_5 (
    .in0(multiplexer_4_out), .in1(shr_max_helper_cs25b018_cs25b095_1_y), .out(Y_16), .sel(SHR_5[4]));
endmodule

module shl_max_helper_CS25B018_CS25B095 (
  input  [15:0] A,
  output [15:0] Y
);

  assign Y = A & {16{1'b0}};  // AND_Gate and_1, 16 bits wide

  // Notes on the sheet:
  //   CONST_0
endmodule

module shr_max_helper_CS25B018_CS25B095 (
  input  [15:0] A,
  output [15:0] Y
);

  assign Y = A & {16{1'b0}};  // AND_Gate and_1, 16 bits wide

  // Notes on the sheet:
  //   CONST_0
endmodule

module one_bit_comp_helper_CS25B018_CS25B095 (
  input  A,
  input  B,
  input  GTin,
  input  EQin,
  input  LTin,
  output GT,
  output EQ,
  output LT
);

  wire demultiplexer_1_out1, demultiplexer_2_out0, demultiplexer_2_out1, xor_1_out;

  Demultiplexer demultiplexer_1 (.out0(EQ), .out1(demultiplexer_1_out1), .in(EQin), .sel(xor_1_out));
  xor xor_1 (xor_1_out, A, B);
  Demultiplexer demultiplexer_2 (
    .out0(demultiplexer_2_out0), .out1(demultiplexer_2_out1), .in(demultiplexer_1_out1), .sel(B));
  Multiplexer multiplexer_1 (.in0(demultiplexer_2_out0), .in1(GTin), .out(GT), .sel(GTin));
  Multiplexer multiplexer_2 (.in0(demultiplexer_2_out1), .in1(LTin), .out(LT), .sel(LTin));
endmodule

module cmp4_CS25B018_CS25B095 (
  input  [3:0] A,
  input  [3:0] B,
  input  GTin,
  input  EQin,
  input  LTin,
  output GT,
  output EQ,
  output LT
);

  wire one_bit_comp_helper_cs25b018_cs25b095_1_eq, one_bit_comp_helper_cs25b018_cs25b095_1_gt,
       one_bit_comp_helper_cs25b018_cs25b095_1_lt, one_bit_comp_helper_cs25b018_cs25b095_2_eq,
       one_bit_comp_helper_cs25b018_cs25b095_2_gt, one_bit_comp_helper_cs25b018_cs25b095_2_lt,
       one_bit_comp_helper_cs25b018_cs25b095_3_eq, one_bit_comp_helper_cs25b018_cs25b095_3_gt,
       one_bit_comp_helper_cs25b018_cs25b095_3_lt;

  one_bit_comp_helper_CS25B018_CS25B095 one_bit_comp_helper_cs25b018_cs25b095_1 (
    .A(A[3]), .B(B[3]), .GTin(GTin), .EQin(EQin), .LTin(LTin),
    .GT(one_bit_comp_helper_cs25b018_cs25b095_1_gt), .EQ(one_bit_comp_helper_cs25b018_cs25b095_1_eq),
    .LT(one_bit_comp_helper_cs25b018_cs25b095_1_lt));
  one_bit_comp_helper_CS25B018_CS25B095 one_bit_comp_helper_cs25b018_cs25b095_2 (
    .A(A[2]), .B(B[2]), .GTin(one_bit_comp_helper_cs25b018_cs25b095_1_gt),
    .EQin(one_bit_comp_helper_cs25b018_cs25b095_1_eq), .LTin(one_bit_comp_helper_cs25b018_cs25b095_1_lt),
    .GT(one_bit_comp_helper_cs25b018_cs25b095_2_gt), .EQ(one_bit_comp_helper_cs25b018_cs25b095_2_eq),
    .LT(one_bit_comp_helper_cs25b018_cs25b095_2_lt));
  one_bit_comp_helper_CS25B018_CS25B095 one_bit_comp_helper_cs25b018_cs25b095_3 (
    .A(A[1]), .B(B[1]), .GTin(one_bit_comp_helper_cs25b018_cs25b095_2_gt),
    .EQin(one_bit_comp_helper_cs25b018_cs25b095_2_eq), .LTin(one_bit_comp_helper_cs25b018_cs25b095_2_lt),
    .GT(one_bit_comp_helper_cs25b018_cs25b095_3_gt), .EQ(one_bit_comp_helper_cs25b018_cs25b095_3_eq),
    .LT(one_bit_comp_helper_cs25b018_cs25b095_3_lt));
  one_bit_comp_helper_CS25B018_CS25B095 one_bit_comp_helper_cs25b018_cs25b095_4 (
    .A(A[0]), .B(B[0]), .GTin(one_bit_comp_helper_cs25b018_cs25b095_3_gt),
    .EQin(one_bit_comp_helper_cs25b018_cs25b095_3_eq), .LTin(one_bit_comp_helper_cs25b018_cs25b095_3_lt),
    .GT(GT), .EQ(EQ), .LT(LT));
endmodule

module cmp16_CS25B018_CS25B095 (
  input  [15:0] A,
  input  [15:0] B,
  output GT,
  output EQ,
  output LT
);

  wire cmp4_cs25b018_cs25b095_1_eq, cmp4_cs25b018_cs25b095_1_gt, cmp4_cs25b018_cs25b095_1_lt,
       cmp4_cs25b018_cs25b095_2_eq, cmp4_cs25b018_cs25b095_2_gt, cmp4_cs25b018_cs25b095_2_lt,
       cmp4_cs25b018_cs25b095_3_eq, cmp4_cs25b018_cs25b095_3_gt, cmp4_cs25b018_cs25b095_3_lt, not_1_out,
       not_2_out, one_bit_comp_helper_cs25b018_cs25b095_1_eq, one_bit_comp_helper_cs25b018_cs25b095_1_gt,
       one_bit_comp_helper_cs25b018_cs25b095_1_lt;

  cmp4_CS25B018_CS25B095 cmp4_cs25b018_cs25b095_1 (
    .A(A[15:12]), .B(B[15:12]), .GTin(one_bit_comp_helper_cs25b018_cs25b095_1_gt),
    .EQin(one_bit_comp_helper_cs25b018_cs25b095_1_eq), .LTin(one_bit_comp_helper_cs25b018_cs25b095_1_lt),
    .GT(cmp4_cs25b018_cs25b095_1_gt), .EQ(cmp4_cs25b018_cs25b095_1_eq), .LT(cmp4_cs25b018_cs25b095_1_lt));
  not not_1 (not_1_out, A[15]);
  not not_2 (not_2_out, B[15]);
  cmp4_CS25B018_CS25B095 cmp4_cs25b018_cs25b095_2 (
    .A(A[11:8]), .B(B[11:8]), .GTin(cmp4_cs25b018_cs25b095_1_gt), .EQin(cmp4_cs25b018_cs25b095_1_eq),
    .LTin(cmp4_cs25b018_cs25b095_1_lt), .GT(cmp4_cs25b018_cs25b095_2_gt), .EQ(cmp4_cs25b018_cs25b095_2_eq),
    .LT(cmp4_cs25b018_cs25b095_2_lt));
  one_bit_comp_helper_CS25B018_CS25B095 one_bit_comp_helper_cs25b018_cs25b095_1 (
    .A(not_1_out), .B(not_2_out), .GTin(1'b0), .EQin(1'b1), .LTin(1'b0),
    .GT(one_bit_comp_helper_cs25b018_cs25b095_1_gt), .EQ(one_bit_comp_helper_cs25b018_cs25b095_1_eq),
    .LT(one_bit_comp_helper_cs25b018_cs25b095_1_lt));
  cmp4_CS25B018_CS25B095 cmp4_cs25b018_cs25b095_3 (
    .A(A[7:4]), .B(B[7:4]), .GTin(cmp4_cs25b018_cs25b095_2_gt), .EQin(cmp4_cs25b018_cs25b095_2_eq),
    .LTin(cmp4_cs25b018_cs25b095_2_lt), .GT(cmp4_cs25b018_cs25b095_3_gt), .EQ(cmp4_cs25b018_cs25b095_3_eq),
    .LT(cmp4_cs25b018_cs25b095_3_lt));
  cmp4_CS25B018_CS25B095 cmp4_cs25b018_cs25b095_4 (
    .A(A[3:0]), .B(B[3:0]), .GTin(cmp4_cs25b018_cs25b095_3_gt), .EQin(cmp4_cs25b018_cs25b095_3_eq),
    .LTin(cmp4_cs25b018_cs25b095_3_lt), .GT(GT), .EQ(EQ), .LT(LT));
endmodule

module logic_unit_CS25B018_CS25B095 (
  input  [15:0] A,
  input  [15:0] B,
  output [15:0] AND_LOGIC,
  output [15:0] OR_LOGIC,
  output [15:0] XOR_LOGIC,
  output [15:0] NOT_LOGIC
);

  assign AND_LOGIC = A & B;  // AND_Gate and_1, 16 bits wide
  assign OR_LOGIC = A | B;  // OR_Gate or_1, 16 bits wide
  assign XOR_LOGIC = A ^ B;  // XOR_Gate xor_1, 16 bits wide
  assign NOT_LOGIC = ~A;  // NOT_Gate not_1, 16 bits wide
endmodule

module alu_CS25B018_CS25B095 (
  input  [4:0] OPCODE,
  input  [15:0] A,
  input  [15:0] B,
  input  ALU_OUTPUT_ENABLE,
  output Z,
  output N,
  output C,
  output V,
  output [15:0] BUS_OUT
);

  wire addsub16_cs25b018_cs25b095_1_cout, addsub16_cs25b018_cs25b095_1_ovf,
       addsub16_cs25b018_cs25b095_2_cout, addsub16_cs25b018_cs25b095_2_ovf, and_1_out, and_2_out, and_3_out,
       and_4_out, cmp16_cs25b018_cs25b095_1_lt, cmp16_cs25b018_cs25b095_2_eq, cmp16_cs25b018_cs25b095_3_eq;
  wire [15:0] addsub16_cs25b018_cs25b095_1_s, addsub16_cs25b018_cs25b095_2_s, bit_extender_1_out,
       bit_extender_2_out, bit_extender_3_out, logic_unit_cs25b018_cs25b095_1_and_logic,
       logic_unit_cs25b018_cs25b095_1_not_logic, logic_unit_cs25b018_cs25b095_1_or_logic,
       logic_unit_cs25b018_cs25b095_1_xor_logic, multiplexer_1_out, multiplexer_2_out, multiplexer_3_out,
       multiplexer_4_out, multiplexer_5_out, multiplexer_6_out, multiplexer_7_out, multiplexer_8_out,
       multiplexer_9_out, multiplexer_10_out, multiplexer_11_out, multiplexer_12_out, multiplexer_13_out,
       multiplexer_14_out, multiplexer_15_out, multiplexer_16_out, multiplexer_17_out, multiplexer_18_out,
       multiplexer_19_out, multiplexer_20_out, multiplexer_21_out, multiplexer_22_out, multiplexer_23_out,
       multiplexer_24_out, multiplexer_25_out, multiplexer_26_out, multiplexer_27_out, multiplexer_28_out,
       multiplexer_29_out, multiplexer_30_out, multiplexer_31_out, shl16_cs25b018_cs25b095_1_y_16,
       shr16_cs25b018_cs25b095_1_y_16;

  addsub16_CS25B018_CS25B095 addsub16_cs25b018_cs25b095_1 (
    .A(A), .B(B), .SUB(1'b0), .S(addsub16_cs25b018_cs25b095_1_s), .COUT(addsub16_cs25b018_cs25b095_1_cout),
    .OVF(addsub16_cs25b018_cs25b095_1_ovf));
  addsub16_CS25B018_CS25B095 addsub16_cs25b018_cs25b095_2 (
    .A(A), .B(B), .SUB(1'b1), .S(addsub16_cs25b018_cs25b095_2_s), .COUT(addsub16_cs25b018_cs25b095_2_cout),
    .OVF(addsub16_cs25b018_cs25b095_2_ovf));
  logic_unit_CS25B018_CS25B095 logic_unit_cs25b018_cs25b095_1 (
    .A(A), .B(B), .AND_LOGIC(logic_unit_cs25b018_cs25b095_1_and_logic),
    .OR_LOGIC(logic_unit_cs25b018_cs25b095_1_or_logic), .XOR_LOGIC(logic_unit_cs25b018_cs25b095_1_xor_logic),
    .NOT_LOGIC(logic_unit_cs25b018_cs25b095_1_not_logic));
  shl16_CS25B018_CS25B095 shl16_cs25b018_cs25b095_1 (.A(A), .SHL_5(B[4:0]), .Y_16(shl16_cs25b018_cs25b095_1_y_16));
  shr16_CS25B018_CS25B095 shr16_cs25b018_cs25b095_1 (.A(A), .SHR_5(B[4:0]), .Y_16(shr16_cs25b018_cs25b095_1_y_16));
  cmp16_CS25B018_CS25B095 cmp16_cs25b018_cs25b095_1 (.A(A), .B(B), .LT(cmp16_cs25b018_cs25b095_1_lt));  // open: GT, EQ
  assign bit_extender_1_out = {{15{1'b0}}, cmp16_cs25b018_cs25b095_1_lt};  // Bit_Extender bit_extender_1
  assign bit_extender_2_out = {{11{1'b0}}, OPCODE};  // Bit_Extender bit_extender_2
  assign bit_extender_3_out = {{11{1'b0}}, OPCODE};  // Bit_Extender bit_extender_3
  Multiplexer #(.width(16)) multiplexer_1 (
    .in0({16{1'b0}}), .in1({16{1'b0}}), .out(multiplexer_1_out), .sel(OPCODE[0]));
  Multiplexer #(.width(16)) multiplexer_2 (
    .in0({16{1'b0}}), .in1({16{1'b0}}), .out(multiplexer_2_out), .sel(OPCODE[0]));
  Multiplexer #(.width(16)) multiplexer_3 (
    .in0({16{1'b0}}), .in1({16{1'b0}}), .out(multiplexer_3_out), .sel(OPCODE[0]));
  Multiplexer #(.width(16)) multiplexer_4 (
    .in0({16{1'b0}}), .in1({16{1'b0}}), .out(multiplexer_4_out), .sel(OPCODE[0]));
  Multiplexer #(.width(16)) multiplexer_5 (
    .in0({16{1'b0}}), .in1(addsub16_cs25b018_cs25b095_1_s), .out(multiplexer_5_out), .sel(OPCODE[0]));
  Multiplexer #(.width(16)) multiplexer_6 (
    .in0(addsub16_cs25b018_cs25b095_2_s), .in1({16{1'b0}}), .out(multiplexer_6_out), .sel(OPCODE[0]));
  Multiplexer #(.width(16)) multiplexer_7 (
    .in0({16{1'b0}}), .in1(logic_unit_cs25b018_cs25b095_1_and_logic), .out(multiplexer_7_out), .sel(OPCODE[0]));
  Multiplexer #(.width(16)) multiplexer_8 (
    .in0(logic_unit_cs25b018_cs25b095_1_or_logic), .in1(logic_unit_cs25b018_cs25b095_1_xor_logic),
    .out(multiplexer_8_out), .sel(OPCODE[0]));
  Multiplexer #(.width(16)) multiplexer_9 (
    .in0(logic_unit_cs25b018_cs25b095_1_not_logic), .in1(shl16_cs25b018_cs25b095_1_y_16),
    .out(multiplexer_9_out), .sel(OPCODE[0]));
  Multiplexer #(.width(16)) multiplexer_10 (
    .in0(shr16_cs25b018_cs25b095_1_y_16), .in1(bit_extender_1_out), .out(multiplexer_10_out), .sel(OPCODE[0]));
  Multiplexer #(.width(16)) multiplexer_11 (
    .in0({16{1'b0}}), .in1({16{1'b0}}), .out(multiplexer_11_out), .sel(OPCODE[0]));
  Multiplexer #(.width(16)) multiplexer_12 (
    .in0({16{1'b0}}), .in1({16{1'b0}}), .out(multiplexer_12_out), .sel(OPCODE[0]));
  Multiplexer #(.width(16)) multiplexer_13 (
    .in0({16{1'b0}}), .in1({16{1'b0}}), .out(multiplexer_13_out), .sel(OPCODE[0]));
  Multiplexer #(.width(16)) multiplexer_14 (
    .in0({16{1'b0}}), .in1({16{1'b0}}), .out(multiplexer_14_out), .sel(OPCODE[0]));
  Multiplexer #(.width(16)) multiplexer_15 (
    .in0({16{1'b0}}), .in1({16{1'b0}}), .out(multiplexer_15_out), .sel(OPCODE[0]));
  Multiplexer #(.width(16)) multiplexer_16 (
    .in0({16{1'b0}}), .in1({16{1'b0}}), .out(multiplexer_16_out), .sel(OPCODE[0]));
  Multiplexer #(.width(16)) multiplexer_17 (
    .in0(multiplexer_1_out), .in1(multiplexer_2_out), .out(multiplexer_17_out), .sel(OPCODE[1]));
  Multiplexer #(.width(16)) multiplexer_18 (
    .in0(multiplexer_3_out), .in1(multiplexer_4_out), .out(multiplexer_18_out), .sel(OPCODE[1]));
  Multiplexer #(.width(16)) multiplexer_19 (
    .in0(multiplexer_5_out), .in1(multiplexer_6_out), .out(multiplexer_19_out), .sel(OPCODE[1]));
  Multiplexer #(.width(16)) multiplexer_20 (
    .in0(multiplexer_7_out), .in1(multiplexer_8_out), .out(multiplexer_20_out), .sel(OPCODE[1]));
  Multiplexer #(.width(16)) multiplexer_21 (
    .in0(multiplexer_9_out), .in1(multiplexer_10_out), .out(multiplexer_21_out), .sel(OPCODE[1]));
  Multiplexer #(.width(16)) multiplexer_22 (
    .in0(multiplexer_11_out), .in1(multiplexer_12_out), .out(multiplexer_22_out), .sel(OPCODE[1]));
  Multiplexer #(.width(16)) multiplexer_23 (
    .in0(multiplexer_13_out), .in1(multiplexer_14_out), .out(multiplexer_23_out), .sel(OPCODE[1]));
  Multiplexer #(.width(16)) multiplexer_24 (
    .in0(multiplexer_15_out), .in1(multiplexer_16_out), .out(multiplexer_24_out), .sel(OPCODE[1]));
  Multiplexer #(.width(16)) multiplexer_25 (
    .in0(multiplexer_17_out), .in1(multiplexer_18_out), .out(multiplexer_25_out), .sel(OPCODE[2]));
  Multiplexer #(.width(16)) multiplexer_26 (
    .in0(multiplexer_19_out), .in1(multiplexer_20_out), .out(multiplexer_26_out), .sel(OPCODE[2]));
  Multiplexer #(.width(16)) multiplexer_27 (
    .in0(multiplexer_21_out), .in1(multiplexer_22_out), .out(multiplexer_27_out), .sel(OPCODE[2]));
  Multiplexer #(.width(16)) multiplexer_28 (
    .in0(multiplexer_23_out), .in1(multiplexer_24_out), .out(multiplexer_28_out), .sel(OPCODE[2]));
  Multiplexer #(.width(16)) multiplexer_29 (
    .in0(multiplexer_25_out), .in1(multiplexer_26_out), .out(multiplexer_29_out), .sel(OPCODE[3]));
  Multiplexer #(.width(16)) multiplexer_30 (
    .in0(multiplexer_27_out), .in1(multiplexer_28_out), .out(multiplexer_30_out), .sel(OPCODE[3]));
  cmp16_CS25B018_CS25B095 cmp16_cs25b018_cs25b095_2 (
    .A(16'h9), .B(bit_extender_2_out), .EQ(cmp16_cs25b018_cs25b095_2_eq));  // open: GT, LT
  Multiplexer #(.width(16)) multiplexer_31 (
    .in0(multiplexer_29_out), .in1(multiplexer_30_out), .out(multiplexer_31_out), .sel(OPCODE[4]));
  assign BUS_OUT = ALU_OUTPUT_ENABLE ? multiplexer_31_out : 16'bz;  // Controlled_Buffer controlled_buffer_1
  cmp16_CS25B018_CS25B095 cmp16_cs25b018_cs25b095_3 (
    .A(16'ha), .B(bit_extender_3_out), .EQ(cmp16_cs25b018_cs25b095_3_eq));  // open: GT, LT
  and and_1 (and_1_out, cmp16_cs25b018_cs25b095_3_eq, addsub16_cs25b018_cs25b095_2_cout);
  and and_2 (and_2_out, cmp16_cs25b018_cs25b095_3_eq, addsub16_cs25b018_cs25b095_2_ovf);
  and and_3 (and_3_out, cmp16_cs25b018_cs25b095_2_eq, addsub16_cs25b018_cs25b095_1_cout);
  and and_4 (and_4_out, cmp16_cs25b018_cs25b095_2_eq, addsub16_cs25b018_cs25b095_1_ovf);
  cmp16_CS25B018_CS25B095 cmp16_cs25b018_cs25b095_4 (
    .A(multiplexer_31_out), .B({16{1'b0}}), .EQ(Z), .LT(N));  // open: GT
  or or_1 (C, and_1_out, and_3_out);
  or or_2 (V, and_2_out, and_4_out);

  // Notes on the sheet:
  //   op_9
  //   op_10
  //   op_13-16
  //   op_17
  //   op_18
  //   op_19
  //   op_20-32
  //   0-1
  //   2-3
  //   4-5
  //   6-7
  //   8-9
  //   10-11
  //   12-13
  //   14-15
  //   16-17
  //   18-19
  //   20-21
  //   22-23
  //   24-25
  //   26-27
  //   28-29
  //   30-31
  //   0-3
  //   4-7
  //   8-11
  //   12-15
  //   16-19
  //   24-27
  //   28-31
  //   20-23
  //   0-7
  //   8-15
endmodule
