// Logisim project G06_th3_storage.circ as structural Verilog: 11 circuits, main circuit main
module main (
  input  [15:0] FETCH_PC,
  input  FETCH_EN,
  input  MAR_EN,
  input  MAR_ALU_EN,
  input  W_EN,
  input  R_EN,
  input  CLK,
  input  RST,
  input  MDR_EN,
  input  MDR_ALU_LOAD,
  input  IR_LOAD,
  input  [15:0] ALU_OUT,
  output [15:0] PC_OP,
  output [15:0] MAR_OP,
  output [15:0] RAM_OP,
  output [15:0] MDR_OP,
  output [15:0] IR_OP
);

  architectural_registers_CS25B018_CS25B095 architectural_registers_cs25b018_cs25b095_1 (
    .FETCH_PC(FETCH_PC), .FETCH_EN(FETCH_EN), .MAR_EN(MAR_EN), .MAR_ALU_EN(MAR_ALU_EN), .WRITE_EN(W_EN),
    .READ_EN(R_EN), .CLK(CLK), .RST(RST), .MDR_EN(MDR_EN), .MDR_ALU_LOAD(MDR_ALU_LOAD), .IR_LOAD(IR_LOAD),
    .ALU_OUT(ALU_OUT), .PC_OP(PC_OP), .MAR_OP(MAR_OP), .ram_word_op(RAM_OP), .MDR_OP(MDR_OP), .IR_OUT(IR_OP));
endmodule

module dff_CS25B018_CS25B095 (
  input  D,
  input  CLK,
  input  EN,
  input  RST,
  output Q
);

  wire multiplexer_1_out;

  Multiplexer multiplexer_1 (.in0(Q), .in1(D), .out(multiplexer_1_out), .sel(EN));
  D_Flip_Flop d_ff_1 (.D(multiplexer_1_out), .clk(CLK), .Q(Q), .reset(RST));  // open: Qn, preset
endmodule

module register16_CS25B018_CS25B095 (
  input  [15:0] D,
  input  CLK,
  input  LOAD,
  input  RST,
  output [15:0] Q
);

  dff_CS25B018_CS25B095 dff_cs25b018_cs25b095_1 (.D(D[0]), .CLK(CLK), .EN(LOAD), .RST(RST), .Q(Q[0]));
  dff_CS25B018_CS25B095 dff_cs25b018_cs25b095_2 (.D(D[1]), .CLK(CLK), .EN(LOAD), .RST(RST), .Q(Q[1]));
  dff_CS25B018_CS25B095 dff_cs25b018_cs25b095_3 (.D(D[2]), .CLK(CLK), .EN(LOAD), .RST(RST), .Q(Q[2]));
  dff_CS25B018_CS25B095 dff_cs25b018_cs25b095_4 (.D(D[3]), .CLK(CLK), .EN(LOAD), .RST(RST), .Q(Q[3]));
  dff_CS25B018_CS25B095 dff_cs25b018_cs25b095_5 (.D(D[4]), .CLK(CLK), .EN(LOAD), .RST(RST), .Q(Q[4]));
  dff_CS25B018_CS25B095 dff_cs25b018_cs25b095_6 (.D(D[5]), .CLK(CLK), .EN(LOAD), .RST(RST), .Q(Q[5]));
  dff_CS25B018_CS25B095 dff_cs25b018_cs25b095_7 (.D(D[6]), .CLK(CLK), .EN(LOAD), .RST(RST), .Q(Q[6]));
  dff_CS25B018_CS25B095 dff_cs25b018_cs25b095_8 (.D(D[7]), .CLK(CLK), .EN(LOAD), .RST(RST), .Q(Q[7]));
  dff_CS25B018_CS25B095 dff_cs25b018_cs25b095_9 (.D(D[8]), .CLK(CLK), .EN(LOAD), .RST(RST), .Q(Q[8]));
  dff_CS25B018_CS25B095 dff_cs25b018_cs25b095_10 (.D(D[9]), .CLK(CLK), .EN(LOAD), .RST(RST), .Q(Q[9]));
  dff_CS25B018_CS25B095 dff_cs25b018_cs25b095_11 (.D(D[10]), .CLK(CLK), .EN(LOAD), .RST(RST), .Q(Q[10]));
  dff_CS25B018_CS25B095 dff_cs25b018_cs25b095_12 (.D(D[11]), .CLK(CLK), .EN(LOAD), .RST(RST), .Q(Q[11]));
  dff_CS25B018_CS25B095 dff_cs25b018_cs25b095_13 (.D(D[12]), .CLK(CLK), .EN(LOAD), .RST(RST), .Q(Q[12]));
  dff_CS25B018_CS25B095 dff_cs25b018_cs25b095_14 (.D(D[13]), .CLK(CLK), .EN(LOAD), .RST(RST), .Q(Q[13]));
  dff_CS25B018_CS25B095 dff_cs25b018_cs25b095_15 (.D(D[14]), .CLK(CLK), .EN(LOAD), .RST(RST), .Q(Q[14]));
  dff_CS25B018_CS25B095 dff_cs25b018_cs25b095_16 (.D(D[15]), .CLK(CLK), .EN(LOAD), .RST(RST), .Q(Q[15]));
endmodule

module regfile8x16_CS25B018_CS25B095 (
  input  RA_en,
  input  [2:0] RA,
  input  RB_en,
  input  [2:0] RB,
  input  [2:0] RD,
  input  [15:0] D,
  input  WE,
  input  CLK,
  input  RST,
  input  EXT,
  output [15:0] R0,
  output [15:0] R1,
  output [15:0] R2,
  output [15:0] R3,
  output [15:0] R4,
  output [15:0] R5,
  output [15:0] R6,
  output [15:0] R7,
  output [15:0] QA,
  output [15:0] QB
);

  wire decoder_1_out0, decoder_1_out1, decoder_1_out2, decoder_1_out3, decoder_1_out4, decoder_1_out5,
       decoder_1_out6, decoder_1_out7, decoder_2_out0, decoder_2_out1, decoder_2_out2, decoder_2_out3,
       decoder_2_out4, decoder_2_out5, decoder_2_out6, decoder_2_out7, decoder_3_out0, decoder_3_out1,
       decoder_3_out2, decoder_3_out3, decoder_3_out4, decoder_3_out5, decoder_3_out6, decoder_3_out7;
  wire [15:0] multiplexer_1_out;

  Multiplexer #(.width(16)) multiplexer_1 (.in0(QA), .in1(D), .out(multiplexer_1_out), .sel(EXT));
  Decoder #(.select(3)) decoder_1 (
    .out0(decoder_1_out0), .out1(decoder_1_out1), .out2(decoder_1_out2), .out3(decoder_1_out3),
    .out4(decoder_1_out4), .out5(decoder_1_out5), .out6(decoder_1_out6), .out7(decoder_1_out7), .sel(RD),
    .en(WE));
  register16_CS25B018_CS25B095 register16_cs25b018_cs25b095_1 (
    .D(multiplexer_1_out), .CLK(CLK), .LOAD(decoder_1_out0), .RST(RST), .Q(R0));
  register16_CS25B018_CS25B095 register16_cs25b018_cs25b095_2 (
    .D(multiplexer_1_out), .CLK(CLK), .LOAD(decoder_1_out1), .RST(RST), .Q(R1));
  register16_CS25B018_CS25B095 register16_cs25b018_cs25b095_3 (
    .D(multiplexer_1_out), .CLK(CLK), .LOAD(decoder_1_out2), .RST(RST), .Q(R2));
  register16_CS25B018_CS25B095 register16_cs25b018_cs25b095_4 (
    .D(multiplexer_1_out), .CLK(CLK), .LOAD(decoder_1_out3), .RST(RST), .Q(R3));
  register16_CS25B018_CS25B095 register16_cs25b018_cs25b095_5 (
    .D(multiplexer_1_out), .CLK(CLK), .LOAD(decoder_1_out4), .RST(RST), .Q(R4));
  register16_CS25B018_CS25B095 register16_cs25b018_cs25b095_6 (
    .D(multiplexer_1_out), .CLK(CLK), .LOAD(decoder_1_out5), .RST(RST), .Q(R5));
  register16_CS25B018_CS25B095 register16_cs25b018_cs25b095_7 (
    .D(multiplexer_1_out), .CLK(CLK), .LOAD(decoder_1_out6), .RST(RST), .Q(R6));
  register16_CS25B018_CS25B095 register16_cs25b018_cs25b095_8 (
    .D(multiplexer_1_out), .CLK(CLK), .LOAD(decoder_1_out7), .RST(RST), .Q(R7));
  assign QA = decoder_2_out0 ? R0 : 16'bz;  // Controlled_Buffer controlled_buffer_1
  assign QA = decoder_2_out1 ? R1 : 16'bz;  // Controlled_Buffer controlled_buffer_2
  assign QA = decoder_2_out2 ? R2 : 16'bz;  // Controlled_Buffer controlled_buffer_3
  assign QA = decoder_2_out3 ? R3 : 16'bz;  // Controlled_Buffer controlled_buffer_4
  assign QA = decoder_2_out4 ? R4 : 16'bz;  // Controlled_Buffer controlled_buffer_5
  assign QA = decoder_2_out5 ? R5 : 16'bz;  // Controlled_Buffer controlled_buffer_6
  assign QA = decoder_2_out6 ? R6 : 16'bz;  // Controlled_Buffer controlled_buffer_7
  assign QA = decoder_2_out7 ? R7 : 16'bz;  // Controlled_Buffer controlled_buffer_8
  Decoder #(.select(3)) decoder_2 (
    .out0(decoder_2_out0), .out1(decoder_2_out1), .out2(decoder_2_out2), .out3(decoder_2_out3),
    .out4(decoder_2_out4), .out5(decoder_2_out5), .out6(decoder_2_out6), .out7(decoder_2_out7), .sel(RA),
    .en(RA_en));
  Decoder #(.select(3)) decoder_3 (
    .out0(decoder_3_out0), .out1(decoder_3_out1), .out2(decoder_3_out2), .out3(decoder_3_out3),
    .out4(decoder_3_out4), .out5(decoder_3_out5), .out6(decoder_3_out6), .out7(decoder_3_out7), .sel(RB),
    .en(RB_en));
  assign QB = decoder_3_out0 ? R0 : 16'bz;  // Controlled_Buffer controlled_buffer_9
  assign QB = decoder_3_out1 ? R1 : 16'bz;  // Controlled_Buffer controlled_buffer_10
  assign QB = decoder_3_out2 ? R2 : 16'bz;  // Controlled_Buffer controlled_buffer_11
  assign QB = decoder_3_out3 ? R3 : 16'bz;  // Controlled_Buffer controlled_buffer_12
  assign QB = decoder_3_out4 ? R4 : 16'bz;  // Controlled_Buffer controlled_buffer_13
  assign QB = decoder_3_out5 ? R5 : 16'bz;  // Controlled_Buffer controlled_buffer_14
  assign QB = decoder_3_out6 ? R6 : 16'bz;  // Controlled_Buffer controlled_buffer_15
  assign QB = decoder_3_out7 ? R7 : 16'bz;  // Controlled_Buffer controlled_buffer_16
endmodule

module status_reg_CS25B018_CS25B095 (
  input  Z_IN,
  input  N_IN,
  input  C_IN,
  input  V_IN,
  input  STATUS_WE,
  input  CLK,
  input  RST,
  output Z,
  output N,
  output C,
  output V
);

  wire controlled_buffer_1_out, controlled_buffer_2_out, controlled_buffer_3_out, controlled_buffer_4_out;

  assign controlled_buffer_1_out = STATUS_WE ? C_IN : 1'bz;  // Controlled_Buffer controlled_buffer_1
  assign controlled_buffer_2_out = STATUS_WE ? V_IN : 1'bz;  // Controlled_Buffer controlled_buffer_2
  assign controlled_buffer_3_out = STATUS_WE ? Z_IN : 1'bz;  // Controlled_Buffer controlled_buffer_3
  assign controlled_buffer_4_out = STATUS_WE ? N_IN : 1'bz;  // Controlled_Buffer controlled_buffer_4
  D_Flip_Flop d_ff_1 (.D(controlled_buffer_3_out), .clk(CLK), .Q(Z), .reset(RST));  // open: Qn, preset
  D_Flip_Flop d_ff_2 (.D(controlled_buffer_4_out), .clk(CLK), .Q(N), .reset(RST));  // open: Qn, preset
  D_Flip_Flop d_ff_3 (.D(controlled_buffer_1_out), .clk(CLK), .Q(C), .reset(RST));  // open: Qn, preset
  D_Flip_Flop d_ff_4 (.D(controlled_buffer_2_out), .clk(CLK), .Q(V), .reset(RST));  // open: Qn, preset
endmodule

module PC_CS25B018_CS25B095 (
  input  [15:0] FETCH,
  input  CLK,
  input  FETCH_EN,
  input  RST,
  output [15:0] P_C
);

  wire [15:0] adder_1_out, multiplexer_1_out;

  Multiplexer #(.width(16)) multiplexer_1 (.in0(adder_1_out), .in1(FETCH), .out(multiplexer_1_out), .sel(FETCH_EN));
  register16_CS25B018_CS25B095 register16_cs25b018_cs25b095_1 (
    .D(multiplexer_1_out), .CLK(CLK), .LOAD(1'b1), .RST(RST), .Q(P_C));
  Adder #(.width(16)) adder_1 (.a(P_C), .b(16'h2), .out(adder_1_out));  // open: cin, cout
endmodule

module MAR_CS25B018_CS25B095 (
  input  [15:0] FROM_PC,
  input  [15:0] FROM_ALU,
  input  CLK,
  input  MAR_LOAD,
  input  ALU_EN,
  input  RST,
  output [15:0] MAR_OP
);

  wire [15:0] multiplexer_1_out;

  Multiplexer #(.width(16)) multiplexer_1 (.in0(FROM_PC), .in1(FROM_ALU), .out(multiplexer_1_out), .sel(ALU_EN));
  register16_CS25B018_CS25B095 register16_cs25b018_cs25b095_1 (
    .D(multiplexer_1_out), .CLK(CLK), .LOAD(MAR_LOAD), .RST(RST), .Q(MAR_OP));
endmodule

module MDR_CS25B018_CS25B095 (
  input  [15:0] MEM,
  input  [15:0] ALU,
  input  CLK,
  input  MDR_LOAD,
  input  RST,
  input  ALU_EN,
  output [15:0] MDR_OUT
);

  wire [15:0] multiplexer_1_out;

  Multiplexer #(.width(16)) multiplexer_1 (.in0(MEM), .in1(ALU), .out(multiplexer_1_out), .sel(ALU_EN));
  register16_CS25B018_CS25B095 register16_cs25b018_cs25b095_1 (
    .D(multiplexer_1_out), .CLK(CLK), .LOAD(MDR_LOAD), .RST(RST), .Q(MDR_OUT));
endmodule

module IR_CS25B018_CS25B095 (
  input  [15:0] MDR_OUT,
  input  CLK,
  input  IR_LOAD,
  input  RST,
  output [15:0] IR_OUT
);

  register16_CS25B018_CS25B095 register16_cs25b018_cs25b095_1 (
    .D(MDR_OUT), .CLK(CLK), .LOAD(IR_LOAD), .RST(RST), .Q(IR_OUT));
endmodule

module ram_word_CS25B018_CS25B095 (
  input  [15:0] ADDR,
  input  [15:0] DIN,
  input  MEM_WRITE,
  input  MEM_READ,
  input  CLK,
  output [15:0] DOUT
);

  RAM #(.addrWidth(15), .dataWidth(16)) ram_1 (
    .addr(ADDR[15:1]), .we(MEM_WRITE), .oe(MEM_READ), .clk(CLK), .din(DIN), .dout(DOUT));
endmodule

module architectural_registers_CS25B018_CS25B095 (
  input  [15:0] FETCH_PC,
  input  FETCH_EN,
  input  MAR_EN,
  input  MAR_ALU_EN,
  input  WRITE_EN,
  input  READ_EN,
  input  CLK,
  input  RST,
  input  MDR_EN,
  input  MDR_ALU_LOAD,
  input  IR_LOAD,
  input  [15:0] ALU_OUT,
  output [15:0] PC_OP,
  output [15:0] MAR_OP,
  output [15:0] ram_word_op,
  output [15:0] MDR_OP,
  output [15:0] IR_OUT
);

  PC_CS25B018_CS25B095 pc_cs25b018_cs25b095_1 (
    .FETCH(FETCH_PC), .CLK(CLK), .FETCH_EN(FETCH_EN), .RST(RST), .P_C(PC_OP));
  MAR_CS25B018_CS25B095 mar_cs25b018_cs25b095_1 (
    .FROM_PC(PC_OP), .FROM_ALU(ALU_OUT), .CLK(CLK), .MAR_LOAD(MAR_EN), .ALU_EN(MAR_ALU_EN), .RST(RST),
    .MAR_OP(MAR_OP));
  ram_word_CS25B018_CS25B095 ram_word_cs25b018_cs25b095_1 (
    .ADDR(MAR_OP), .DIN(MDR_OP), .MEM_WRITE(WRITE_EN), .MEM_READ(READ_EN), .CLK(CLK), .DOUT(ram_word_op));
  MDR_CS25B018_CS25B095 mdr_cs25b018_cs25b095_1 (
    .MEM(ram_word_op), .ALU(ALU_OUT), .CLK(CLK), .MDR_LOAD(MDR_EN), .RST(RST), .ALU_EN(MDR_ALU_LOAD),
    .MDR_OUT(MDR_OP));
  IR_CS25B018_CS25B095 ir_cs25b018_cs25b095_1 (
    .MDR_OUT(MDR_OP), .CLK(CLK), .IR_LOAD(IR_LOAD), .RST(RST), .IR_OUT(IR_OUT));
endmodule
