// Logisim project G06_th5_control.circ as structural Verilog: 43 circuits, main circuit main
module main (
  input  in_1,
  output [3:0] out_2,
  output [15:0] out_3,
  output [15:0] out_4,
  output [15:0] out_5,
  output [15:0] out_6,
  output [15:0] out_7,
  output [15:0] out_8,
  output [15:0] out_9,
  output [15:0] out_10,
  output [15:0] out_11,
  output [15:0] out_12,
  output [15:0] out_13,
  output [15:0] out_14,
  output [15:0] out_15
);

  wire clock_1_out;

  Clock clock_1 (.out(clock_1_out));
  tara_cpu_CS25B018_CS25B095 tara_cpu_cs25b018_cs25b095_1 (
    .CLK(clock_1_out), .RST(in_1), .TSTATE(out_2), .PC_COUNT(out_3), .RAM_WORD(out_4), .MAR_OUT(out_5),
    .MDR_OUT(out_6), .IR_OUT(out_7), .R0(out_8), .R1(out_9), .R2(out_10), .R3(out_11), .R4(out_12),
    .R5(out_13), .R6(out_14), .R7(out_15));
endmodule

module dff_CS25B018_CS25B095 (
  input  D,
  input  CLK,
  input  EN,
  input  RST,
  output Q
);

  wire multiplexer_1_out;

  Multiplexer multiplexer_1 (.in0(Q), .in1(D), .out(multiplexer_1_out), .sel(EN));
  D_Flip_Flop d_ff_1 (.D(multiplexer_1_out), .clk(CLK), .Q(Q), .reset(RST));  // open: Qn, preset
endmodule

module register16_CS25B018_CS25B095 (
  input  [15:0] D,
  input  CLK,
  input  LOAD,
  input  RST,
  output [15:0] Q
);

  dff_CS25B018_CS25B095 dff_cs25b018_cs25b095_1 (.D(D[0]), .CLK(CLK), .EN(LOAD), .RST(RST), .Q(Q[0]));
  dff_CS25B018_CS25B095 dff_cs25b018_cs25b095_2 (.D(D[1]), .CLK(CLK), .EN(LOAD), .RST(RST), .Q(Q[1]));
  dff_CS25B018_CS25B095 dff_cs25b018_cs25b095_3 (.D(D[2]), .CLK(CLK), .EN(LOAD), .RST(RST), .Q(Q[2]));
  dff_CS25B018_CS25B095 dff_cs25b018_cs25b095_4 (.D(D[3]), .CLK(CLK), .EN(LOAD), .RST(RST), .Q(Q[3]));
  dff_CS25B018_CS25B095 dff_cs25b018_cs25b095_5 (.D(D[4]), .CLK(CLK), .EN(LOAD), .RST(RST), .Q(Q[4]));
  dff_CS25B018_CS25B095 dff_cs25b018_cs25b095_6 (.D(D[5]), .CLK(CLK), .EN(LOAD), .RST(RST), .Q(Q[5]));
  dff_CS25B018_CS25B095 dff_cs25b018_cs25b095_7 (.D(D[6]), .CLK(CLK), .EN(LOAD), .RST(RST), .Q(Q[6]));
  dff_CS25B018_CS25B095 dff_cs25b018_cs25b095_8 (.D(D[7]), .CLK(CLK), .EN(LOAD), .RST(RST), .Q(Q[7]));
  dff_CS25B018_CS25B095 dff_cs25b018_cs25b095_9 (.D(D[8]), .CLK(CLK), .EN(LOAD), .RST(RST), .Q(Q[8]));
  dff_CS25B018_CS25B095 dff_cs25b018_cs25b095_10 (.D(D[9]), .CLK(CLK), .EN(LOAD), .RST(RST), .Q(Q[9]));
  dff_CS25B018_CS25B095 dff_cs25b018_cs25b095_11 (.D(D[10]), .CLK(CLK), .EN(LOAD), .RST(RST), .Q(Q[10]));
  dff_CS25B018_CS25B095 dff_cs25b018_cs25b095_12 (.D(D[11]), .CLK(CLK), .EN(LOAD), .RST(RST), .Q(Q[11]));
  dff_CS25B018_CS25B095 dff_cs25b018_cs25b095_13 (.D(D[12]), .CLK(CLK), .EN(LOAD), .RST(RST), .Q(Q[12]));
  dff_CS25B018_CS25B095 dff_cs25b018_cs25b095_14 (.D(D[13]), .CLK(CLK), .EN(LOAD), .RST(RST), .Q(Q[13]));
  dff_CS25B018_CS25B095 dff_cs25b018_cs25b095_15 (.D(D[14]), .CLK(CLK), .EN(LOAD), .RST(RST), .Q(Q[14]));
  dff_CS25B018_CS25B095 dff_cs25b018_cs25b095_16 (.D(D[15]), .CLK(CLK), .EN(LOAD), .RST(RST), .Q(Q[15]));
endmodule

module regfile8x16_CS25B018_CS25B095 (
  input  [2:0] RA,
  input  [2:0] RB,
  input  [2:0] RD,
  input  [15:0] D,
  input  WE,
  input  CLK,
  input  RST,
  output [15:0] QA,
  output [15:0] QB,
  output [15:0] R0,
  output [15:0] R1,
  output [15:0] R2,
  output [15:0] R3,
  output [15:0] R4,
  output [15:0] R5,
  output [15:0] R6,
  output [15:0] R7
);

  wire decoder_1_out0, decoder_1_out1, decoder_1_out2, decoder_1_out3, decoder_1_out4, decoder_1_out5,
       decoder_1_out6, decoder_1_out7, decoder_2_out0, decoder_2_out1, decoder_2_out2, decoder_2_out3,
       decoder_2_out4, decoder_2_out5, decoder_2_out6, decoder_2_out7, decoder_3_out0, decoder_3_out1,
       decoder_3_out2, decoder_3_out3, decoder_3_out4, decoder_3_out5, decoder_3_out6, decoder_3_out7;

  Decoder #(.select(3)) decoder_1 (
    .out0(decoder_1_out0), .out1(decoder_1_out1), .out2(decoder_1_out2), .out3(decoder_1_out3),
    .out4(decoder_1_out4), .out5(decoder_1_out5), .out6(decoder_1_out6), .out7(decoder_1_out7), .sel(RD),
    .en(WE));
  register16_CS25B018_CS25B095 register16_cs25b018_cs25b095_1 (
    .D(D), .CLK(CLK), .LOAD(decoder_1_out0), .RST(RST), .Q(R0));
  register16_CS25B018_CS25B095 register16_cs25b018_cs25b095_2 (
    .D(D), .CLK(CLK), .LOAD(decoder_1_out1), .RST(RST), .Q(R1));
  register16_CS25B018_CS25B095 register16_cs25b018_cs25b095_3 (
    .D(D), .CLK(CLK), .LOAD(decoder_1_out2), .RST(RST), .Q(R2));
  register16_CS25B018_CS25B095 register16_cs25b018_cs25b095_4 (
    .D(D), .CLK(CLK), .LOAD(decoder_1_out3), .RST(RST), .Q(R3));
  register16_CS25B018_CS25B095 register16_cs25b018_cs25b095_5 (
    .D(D), .CLK(CLK), .LOAD(decoder_1_out4), .RST(RST), .Q(R4));
  register16_CS25B018_CS25B095 register16_cs25b018_cs25b095_6 (
    .D(D), .CLK(CLK), .LOAD(decoder_1_out5), .RST(RST), .Q(R5));
  register16_CS25B018_CS25B095 register16_cs25b018_cs25b095_7 (
    .D(D), .CLK(CLK), .LOAD(decoder_1_out6), .RST(RST), .Q(R6));
  register16_CS25B018_CS25B095 register16_cs25b018_cs25b095_8 (
    .D(D), .CLK(CLK), .LOAD(decoder_1_out7), .RST(RST), .Q(R7));
  assign QA = decoder_2_out0 ? R0 : 16'bz;  // Controlled_Buffer controlled_buffer_1
  assign QA = decoder_2_out1 ? R1 : 16'bz;  // Controlled_Buffer controlled_buffer_2
  assign QA = decoder_2_out2 ? R2 : 16'bz;  // Controlled_Buffer controlled_buffer_3
  assign QA = decoder_2_out3 ? R3 : 16'bz;  // Controlled_Buffer controlled_buffer_4
  assign QA = decoder_2_out4 ? R4 : 16'bz;  // Controlled_Buffer controlled_buffer_5
  assign QA = decoder_2_out5 ? R5 : 16'bz;  // Controlled_Buffer controlled_buffer_6
  assign QA = decoder_2_out6 ? R6 : 16'bz;  // Controlled_Buffer controlled_buffer_7
  assign QA = decoder_2_out7 ? R7 : 16'bz;  // Controlled_Buffer controlled_buffer_8
  Decoder #(.select(3)) decoder_2 (
    .out0(decoder_2_out0), .out1(decoder_2_out1), .out2(decoder_2_out2), .out3(decoder_2_out3),
    .out4(decoder_2_out4), .out5(decoder_2_out5), .out6(decoder_2_out6), .out7(decoder_2_out7), .sel(RA),
    .en(1'b1));
  Decoder #(.select(3)) decoder_3 (
    .out0(decoder_3_out0), .out1(decoder_3_out1), .out2(decoder_3_out2), .out3(decoder_3_out3),
    .out4(decoder_3_out4), .out5(decoder_3_out5), .out6(decoder_3_out6), .out7(decoder_3_out7), .sel(RB),
    .en(1'b1));
  assign QB = decoder_3_out0 ? R0 : 16'bz;  // Controlled_Buffer controlled_buffer_9
  assign QB = decoder_3_out1 ? R1 : 16'bz;  // Controlled_Buffer controlled_buffer_10
  assign QB = decoder_3_out2 ? R2 : 16'bz;  // Controlled_Buffer controlled_buffer_11
  assign QB = decoder_3_out3 ? R3 : 16'bz;  // Controlled_Buffer controlled_buffer_12
  assign QB = decoder_3_out4 ? R4 : 16'bz;  // Controlled_Buffer controlled_buffer_13
  assign QB = decoder_3_out5 ? R5 : 16'bz;  // Controlled_Buffer controlled_buffer_14
  assign QB = decoder_3_out6 ? R6 : 16'bz;  // Controlled_Buffer controlled_buffer_15
  assign QB = decoder_3_out7 ? R7 : 16'bz;  // Controlled_Buffer controlled_buffer_16
endmodule

module status_reg_CS25B018_CS25B095 (
  input  Z_IN,
  input  N_IN,
  input  C_IN,
  input  V_IN,
  input  STATUS_WE,
  input  CLK,
  input  RST,
  output Z,
  output N,
  output C,
  output V
);

  wire controlled_buffer_1_out, controlled_buffer_2_out, controlled_buffer_3_out, controlled_buffer_4_out;

  assign controlled_buffer_1_out = STATUS_WE ? C_IN : 1'bz;  // Controlled_Buffer controlled_buffer_1
  assign controlled_buffer_2_out = STATUS_WE ? V_IN : 1'bz;  // Controlled_Buffer controlled_buffer_2
  assign controlled_buffer_3_out = STATUS_WE ? Z_IN : 1'bz;  // Controlled_Buffer controlled_buffer_3
  assign controlled_buffer_4_out = STATUS_WE ? N_IN : 1'bz;  // Controlled_Buffer controlled_buffer_4
  D_Flip_Flop d_ff_1 (.D(controlled_buffer_3_out), .clk(CLK), .Q(Z), .reset(RST));  // open: Qn, preset
  D_Flip_Flop d_ff_2 (.D(controlled_buffer_4_out), .clk(CLK), .Q(N), .reset(RST));  // open: Qn, preset
  D_Flip_Flop d_ff_3 (.D(controlled_buffer_1_out), .clk(CLK), .Q(C), .reset(RST));  // open: Qn, preset
  D_Flip_Flop d_ff_4 (.D(controlled_buffer_2_out), .clk(CLK), .Q(V), .reset(RST));  // open: Qn, preset
endmodule

module PC_CS25B018_CS25B095 (
  input  [15:0] FETCH,
  input  CLK,
  input  PC_LOAD,
  input  FETCH_EN,
  input  RST,
  output [15:0] P_C
);

  wire [15:0] adder_1_out, multiplexer_1_out;

  Multiplexer #(.width(16)) multiplexer_1 (.in0(adder_1_out), .in1(FETCH), .out(multiplexer_1_out), .sel(FETCH_EN));
  register16_CS25B018_CS25B095 register16_cs25b018_cs25b095_1 (
    .D(multiplexer_1_out), .CLK(CLK), .LOAD(PC_LOAD), .RST(RST), .Q(P_C));
  Adder #(.width(16)) adder_1 (.a(P_C), .b(16'h2), .out(adder_1_out));  // open: cin, cout
endmodule

module MAR_CS25B018_CS25B095 (
  input  [15:0] MAR_IN,
  input  CLK,
  input  MAR_LOAD,
  input  RST,
  output [15:0] MAR_OP
);

  register16_CS25B018_CS25B095 register16_cs25b018_cs25b095_1 (
    .D(MAR_IN), .CLK(CLK), .LOAD(MAR_LOAD), .RST(RST), .Q(MAR_OP));
endmodule

module MDR_CS25B018_CS25B095 (
  input  [15:0] MDR_IN,
  input  CLK,
  input  MDR_LOAD,
  input  RST,
  output [15:0] MDR_OUT
);

  register16_CS25B018_CS25B095 register16_cs25b018_cs25b095_1 (
    .D(MDR_IN), .CLK(CLK), .LOAD(MDR_LOAD), .RST(RST), .Q(MDR_OUT));
endmodule

module IR_CS25B018_CS25B095 (
  input  [15:0] MDR_OUT,
  input  CLK,
  input  IR_LOAD,
  input  RST,
  output [15:0] IR_OUT
);

  register16_CS25B018_CS25B095 register16_cs25b018_cs25b095_1 (
    .D(MDR_OUT), .CLK(CLK), .LOAD(IR_LOAD), .RST(RST), .Q(IR_OUT));
endmodule

module ram_word_CS25B018_CS25B095 (
  input  [15:0] ADDR,
  input  [15:0] DIN,
  input  MEM_WRITE,
  input  MEM_READ,
  input  CLK,
  output [15:0] DOUT
);

  RAM #(.addrWidth(15), .dataWidth(16)) ram_1 (
    .addr(ADDR[15:1]), .we(MEM_WRITE), .oe(MEM_READ), .clk(CLK), .din(DIN), .dout(DOUT));
endmodule

module half_adder_CS25B018_CS25B095 (
  input  A,
  input  B,
  output SUM,
  output COUT
);

  xor xor_1 (SUM, A, B);
  and and_1 (COUT, B, A);
endmodule

module full_adder_CS25B018_CS25B095 (
  input  A,
  input  B,
  input  CIN,
  output COUT,
  output SUM
);

  wire half_adder_cs25b018_cs25b095_1_cout, half_adder_cs25b018_cs25b095_1_sum,
       half_adder_cs25b018_cs25b095_2_cout;

  half_adder_CS25B018_CS25B095 half_adder_cs25b018_cs25b095_1 (
    .A(A), .B(B), .SUM(half_adder_cs25b018_cs25b095_1_sum), .COUT(half_adder_cs25b018_cs25b095_1_cout));
  half_adder_CS25B018_CS25B095 half_adder_cs25b018_cs25b095_2 (
    .A(half_adder_cs25b018_cs25b095_1_sum), .B(CIN), .SUM(SUM), .COUT(half_adder_cs25b018_cs25b095_2_cout));
  or or_1 (COUT, half_adder_cs25b018_cs25b095_1_cout, half_adder_cs25b018_cs25b095_2_cout);
endmodule

module adder4_CS25B018_CS25B095 (
  input  CIN,
  input  [3:0] A,
  input  [3:0] B,
  output [3:0] SUM,
  output COUT,
  output LAST_CIN
);

  wire full_adder_cs25b018_cs25b095_1_cout, full_adder_cs25b018_cs25b095_2_cout;

  full_adder_CS25B018_CS25B095 full_adder_cs25b018_cs25b095_1 (
    .A(A[0]), .B(B[0]), .CIN(CIN), .COUT(full_adder_cs25b018_cs25b095_1_cout), .SUM(SUM[0]));
  full_adder_CS25B018_CS25B095 full_adder_cs25b018_cs25b095_2 (
    .A(A[1]), .B(B[1]), .CIN(full_adder_cs25b018_cs25b095_1_cout),
    .COUT(full_adder_cs25b018_cs25b095_2_cout), .SUM(SUM[1]));
  full_adder_CS25B018_CS25B095 full_adder_cs25b018_cs25b095_3 (
    .A(A[2]), .B(B[2]), .CIN(full_adder_cs25b018_cs25b095_2_cout), .COUT(LAST_CIN), .SUM(SUM[2]));
  full_adder_CS25B018_CS25B095 full_adder_cs25b018_cs25b095_4 (
    .A(A[3]), .B(B[3]), .CIN(LAST_CIN), .COUT(COUT), .SUM(SUM[3]));
endmodule

module adder16_CS25B018_CS25B095 (
  input  CIN,
  input  [15:0] A,
  input  [15:0] B,
  output [15:0] S,
  output COUT,
  output LAST_CIN
);

  wire adder4_cs25b018_cs25b095_1_cout, adder4_cs25b018_cs25b095_2_cout, adder4_cs25b018_cs25b095_3_cout;

  adder4_CS25B018_CS25B095 adder4_cs25b018_cs25b095_1 (
    .CIN(CIN), .A(A[3:0]), .B(B[3:0]), .SUM(S[3:0]), .COUT(adder4_cs25b018_cs25b095_1_cout));  // open: LAST_CIN
  adder4_CS25B018_CS25B095 adder4_cs25b018_cs25b095_2 (
    .CIN(adder4_cs25b018_cs25b095_1_cout), .A(A[7:4]), .B(B[7:4]), .SUM(S[7:4]),
    .COUT(adder4_cs25b018_cs25b095_2_cout));  // open: LAST_CIN
  adder4_CS25B018_CS25B095 adder4_cs25b018_cs25b095_3 (
    .CIN(adder4_cs25b018_cs25b095_2_cout), .A(A[11:8]), .B(B[11:8]), .SUM(S[11:8]),
    .COUT(adder4_cs25b018_cs25b095_3_cout));  // open: LAST_CIN
  adder4_CS25B018_CS25B095 adder4_cs25b018_cs25b095_4 (
    .CIN(adder4_cs25b018_cs25b095_3_cout), .A(A[15:12]), .B(B[15:12]), .SUM(S[15:12]), .COUT(COUT),
    .LAST_CIN(LAST_CIN));
endmodule

module xor4_helper_CS25B018_CS25B095 (
  input  [3:0] A,
  input  CIN,
  output [3:0] XOR_A
);

  xor xor_1 (XOR_A[0], A[0], CIN);
  xor xor_2 (XOR_A[1], A[1], CIN);
  xor xor_3 (XOR_A[2], A[2], CIN);
  xor xor_4 (XOR_A[3], A[3], CIN);
endmodule

module xor16_helper_CS25B018_CS25B095 (
  input  [15:0] A,
  input  CIN,
  output [15:0] XOR_A
);

  xor4_helper_CS25B018_CS25B095 xor4_helper_cs25b018_cs25b095_1 (.A(A[3:0]), .CIN(CIN), .XOR_A(XOR_A[3:0]));
  xor4_helper_CS25B018_CS25B095 xor4_helper_cs25b018_cs25b095_2 (.A(A[7:4]), .CIN(CIN), .XOR_A(XOR_A[7:4]));
  xor4_helper_CS25B018_CS25B095 xor4_helper_cs25b018_cs25b095_3 (.A(A[11:8]), .CIN(CIN), .XOR_A(XOR_A[11:8]));
  xor4_helper_CS25B018_CS25B095 xor4_helper_cs25b018_cs25b095_4 (.A(A[15:12]), .CIN(CIN), .XOR_A(XOR_A[15:12]));
endmodule

module addsub16_CS25B018_CS25B095 (
  input  [15:0] A,
  input  [15:0] B,
  input  SUB,
  output [15:0] S,
  output COUT,
  output OVF
);

  wire adder16_cs25b018_cs25b095_1_last_cin;
  wire [15:0] xor16_helper_cs25b018_cs25b095_1_xor_a;

  xor16_helper_CS25B018_CS25B095 xor16_helper_cs25b018_cs25b095_1 (
    .A(B), .CIN(SUB), .XOR_A(xor16_helper_cs25b018_cs25b095_1_xor_a));
  adder16_CS25B018_CS25B095 adder16_cs25b018_cs25b095_1 (
    .CIN(SUB), .A(A), .B(xor16_helper_cs25b018_cs25b095_1_xor_a), .S(S), .COUT(COUT),
    .LAST_CIN(adder16_cs25b018_cs25b095_1_last_cin));
  xor xor_1 (OVF, COUT, adder16_cs25b018_cs25b095_1_last_cin);
endmodule

module shl8_helper_CS25B018_CS25B095 (
  input  [15:0] A,
  output [15:0] Y
);


  assign Y = {A[7:0], {8{1'b0}}};

  // Notes on the sheet:
  //   CONST_0
endmodule

module shl4_helper_CS25B018_CS25B095 (
  input  [15:0] A,
  output [15:0] Y
);


  assign Y = {A[11:0], 4'b0000};

  // Notes on the sheet:
  //   CONST_0
endmodule

module shl2_helper_CS25B018_CS25B095 (
  input  [15:0] A,
  output [15:0] Y
);


  assign Y = {A[13:0], 2'b00};

  // Notes on the sheet:
  //   CONST_0
endmodule

module shl1_helper_CS25B018_CS25B095 (
  input  [15:0] A,
  output [15:0] Y
);


  assign Y = {A[14:0], 1'b0};

  // Notes on the sheet:
  //   CONST_0
endmodule

module shl16_CS25B018_CS25B095 (
  input  [15:0] A,
  input  [4:0] SHL_5,
  output [15:0] Y_16
);

  wire [15:0] multiplexer_1_out, multiplexer_2_out, multiplexer_3_out, multiplexer_4_out,
       shl1_helper_cs25b018_cs25b095_1_y, shl2_helper_cs25b018_cs25b095_1_y,
       shl4_helper_cs25b018_cs25b095_1_y, shl8_helper_cs25b018_cs25b095_1_y,
       shl_max_helper_cs25b018_cs25b095_1_y;

  shl1_helper_CS25B018_CS25B095 shl1_helper_cs25b018_cs25b095_1 (.A(A), .Y(shl1_helper_cs25b018_cs25b095_1_y));
  Multiplexer #(.width(16)) multiplexer_1 (
    .in0(A), .in1(shl1_helper_cs25b018_cs25b095_1_y), .out(multiplexer_1_out), .sel(SHL_5[0]));
  shl2_helper_CS25B018_CS25B095 shl2_helper_cs25b018_cs25b095_1 (
    .A(multiplexer_1_out), .Y(shl2_helper_cs25b018_cs25b095_1_y));
  Multiplexer #(.width(16)) multiplexer_2 (
    .in0(multiplexer_1_out), .in1(shl2_helper_cs25b018_cs25b095_1_y), .out(multiplexer_2_out), .sel(SHL_5[1]));
  shl4_helper_CS25B018_CS25B095 shl4_helper_cs25b018_cs25b095_1 (
    .A(multiplexer_2_out), .Y(shl4_helper_cs25b018_cs25b095_1_y));
  Multiplexer #(.width(16)) multiplexer_3 (
    .in0(multiplexer_2_out), .in1(shl4_helper_cs25b018_cs25b095_1_y), .out(multiplexer_3_out), .sel(SHL_5[2]));
  shl8_helper_CS25B018_CS25B095 shl8_helper_cs25b018_cs25b095_1 (
    .A(multiplexer_3_out), .Y(shl8_helper_cs25b018_cs25b095_1_y));
  Multiplexer #(.width(16)) multiplexer_4 (
    .in0(multiplexer_3_out), .in1(shl8_helper_cs25b018_cs25b095_1_y), .out(multiplexer_4_out), .sel(SHL_5[3]));
  shl_max_helper_CS25B018_CS25B095 shl_max_helper_cs25b018_cs25b095_1 (
    .A(multiplexer_4_out), .Y(shl_max_helper_cs25b018_cs25b095_1_y));
  Multiplexer #(.width(16)) multiplexer_5 (
    .in0(multiplexer_4_out), .in1(shl_max_helper_cs25b018_cs25b095_1_y), .out(Y_16), .sel(SHL_5[4]));
endmodule

module shr8_helper_CS25B018_CS25B095 (
  input  [15:0] A,
  output [15:0] Y
);


  assign Y = {{8{1'b0}}, A[15:8]};

  // Notes on the sheet:
  //   CONST_0
endmodule

module shr4_helper_CS25B018_CS25B095 (
  input  [15:0] A,
  output [15:0] Y
);


  assign Y = {4'b0000, A[15:4]};

  // Notes on the sheet:
  //   CONST_0
endmodule

module shr2_helper_CS25B018_CS25B095 (
  input  [15:0] A,
  output [15:0] Y
);


  assign Y = {2'b00, A[15:2]};

  // Notes on the sheet:
  //   CONST_0
endmodule

module shr1_helper_CS25B018_CS25B095 (
  input  [15:0] A,
  output [15:0] Y
);


  assign Y = {1'b0, A[15:1]};

  // Notes on the sheet:
  //   CONST_0
endmodule

module shr16_CS25B018_CS25B095 (
  input  [15:0] A,
  input  [4:0] SHR_5,
  output [15:0] Y_16
);

  wire [15:0] multiplexer_1_out, multiplexer_2_out, multiplexer_3_out, multiplexer_4_out,
       shr1_helper_cs25b018_cs25b095_1_y, shr2_helper_cs25b018_cs25b095_1_y,
       shr4_helper_cs25b018_cs25b095_1_y, shr8_helper_cs25b018_cs25b095_1_y,
       shr_max_helper_cs25b018_cs25b095_1_y;

  shr1_helper_CS25B018_CS25B095 shr1_helper_cs25b018_cs25b095_1 (.A(A), .Y(shr1_helper_cs25b018_cs25b095_1_y));
  Multiplexer #(.width(16)) multiplexer_1 (
    .in0(A), .in1(shr1_helper_cs25b018_cs25b095_1_y), .out(multiplexer_1_out), .sel(SHR_5[0]));
  shr2_helper_CS25B018_CS25B095 shr2_helper_cs25b018_cs25b095_1 (
    .A(multiplexer_1_out), .Y(shr2_helper_cs25b018_cs25b095_1_y));
  Multiplexer #(.width(16)) multiplexer_2 (
    .in0(multiplexer_1_out), .in1(shr2_helper_cs25b018_cs25b095_1_y), .out(multiplexer_2_out), .sel(SHR_5[1]));
  shr4_helper_CS25B018_CS25B095 shr4_helper_cs25b018_cs25b095_1 (
    .A(multiplexer_2_out), .Y(shr4_helper_cs25b018_cs25b095_1_y));
  Multiplexer #(.width(16)) multiplexer_3 (
    .in0(multiplexer_2_out), .in1(shr4_helper_cs25b018_cs25b095_1_y), .out(multiplexer_3_out), .sel(SHR_5[2]));
  shr8_helper_CS25B018_CS25B095 shr8_helper_cs25b018_cs25b095_1 (
    .A(multiplexer_3_out), .Y(shr8_helper_cs25b018_cs25b095_1_y));
  Multiplexer #(.width(16)) multiplexer_4 (
    .in0(multiplexer_3_out), .in1(shr8_helper_cs25b018_cs25b095_1_y), .out(multiplexer_4_out), .sel(SHR_5[3]));
  shr_max_helper_CS25B018_CS25B095 shr_max_helper_cs25b018_cs25b095_1 (
    .A(multiplexer_4_out), .Y(shr_max_helper_cs25b018_cs25b095_1_y));
  Multiplexer #(.width(16)) multiplexer_5 (
    .in0(multiplexer_4_out), .in1(shr_max_helper_cs25b018_cs25b095_1_y), .out(Y_16), .sel(SHR_5[4]));
endmodule

module shl_max_helper_CS25B018_CS25B095 (
  input  [15:0] A,
  output [15:0] Y
);

  assign Y = A & {16{1'b0}};  // AND_Gate and_1, 16 bits wide

  // Notes on the sheet:
  //   CONST_0
endmodule

module shr_max_helper_CS25B018_CS25B095 (
  input  [15:0] A,
  output [15:0] Y
);

  assign Y = A & {16{1'b0}};  // AND_Gate and_1, 16 bits wide

  // Notes on the sheet:
  //   CONST_0
endmodule

module one_bit_comp_helper_CS25B018_CS25B095 (
  input  A,
  input  B,
  input  GTin,
  input  EQin,
  input  LTin,
  output GT,
  output EQ,
  output LT
);

  wire demultiplexer_1_out1, demultiplexer_2_out0, demultiplexer_2_out1, xor_1_out;

  Demultiplexer demultiplexer_1 (.out0(EQ), .out1(demultiplexer_1_out1), .in(EQin), .sel(xor_1_out));
  xor xor_1 (xor_1_out, A, B);
  Demultiplexer demultiplexer_2 (
    .out0(demultiplexer_2_out0), .out1(demultiplexer_2_out1), .in(demultiplexer_1_out1), .sel(B));
  Multiplexer multiplexer_1 (.in0(demultiplexer_2_out0), .in1(GTin), .out(GT), .sel(GTin));
  Multiplexer multiplexer_2 (.in0(demultiplexer_2_out1), .in1(LTin), .out(LT), .sel(LTin));
endmodule

module cmp4_CS25B018_CS25B095 (
  input  [3:0] A,
  input  [3:0] B,
  input  GTin,
  input  EQin,
  input  LTin,
  output GT,
  output EQ,
  output LT
);

  wire one_bit_comp_helper_cs25b018_cs25b095_1_eq, one_bit_comp_helper_cs25b018_cs25b095_1_gt,
       one_bit_comp_helper_cs25b018_cs25b095_1_lt, one_bit_comp_helper_cs25b018_cs25b095_2_eq,
       one_bit_comp_helper_cs25b018_cs25b095_2_gt, one_bit_comp_helper_cs25b018_cs25b095_2_lt,
       one_bit_comp_helper_cs25b018_cs25b095_3_eq, one_bit_comp_helper_cs25b018_cs25b095_3_gt,
       one_bit_comp_helper_cs25b018_cs25b095_3_lt;

  one_bit_comp_helper_CS25B018_CS25B095 one_bit_comp_helper_cs25b018_cs25b095_1 (
    .A(A[3]), .B(B[3]), .GTin(GTin), .EQin(EQin), .LTin(LTin),
    .GT(one_bit_comp_helper_cs25b018_cs25b095_1_gt), .EQ(one_bit_comp_helper_cs25b018_cs25b095_1_eq),
    .LT(one_bit_comp_helper_cs25b018_cs25b095_1_lt));
  one_bit_comp_helper_CS25B018_CS25B095 one_bit_comp_helper_cs25b018_cs25b095_2 (
    .A(A[2]), .B(B[2]), .GTin(one_bit_comp_helper_cs25b018_cs25b095_1_gt),
    .EQin(one_bit_comp_helper_cs25b018_cs25b095_1_eq), .LTin(one_bit_comp_helper_cs25b018_cs25b095_1_lt),
    .GT(one_bit_comp_helper_cs25b018_cs25b095_2_gt), .EQ(one_bit_comp_helper_cs25b018_cs25b095_2_eq),
    .LT(one_bit_comp_helper_cs25b018_cs25b095_2_lt));
  one_bit_comp_helper_CS25B018_CS25B095 one_bit_comp_helper_cs25b018_cs25b095_3 (
    .A(A[1]), .B(B[1]), .GTin(one_bit_comp_helper_cs25b018_cs25b095_2_gt),
    .EQin(one_bit_comp_helper_cs25b018_cs25b095_2_eq), .LTin(one_bit_comp_helper_cs25b018_cs25b095_2_lt),
    .GT(one_bit_comp_helper_cs25b018_cs25b095_3_gt), .EQ(one_bit_comp_helper_cs25b018_cs25b095_3_eq),
    .LT(one_bit_comp_helper_cs25b018_cs25b095_3_lt));
  one_bit_comp_helper_CS25B018_CS25B095 one_bit_comp_helper_cs25b018_cs25b095_4 (
    .A(A[0]), .B(B[0]), .GTin(one_bit_comp_helper_cs25b018_cs25b095_3_gt),
    .EQin(one_bit_comp_helper_cs25b018_cs25b095_3_eq), .LTin(one_bit_comp_helper_cs25b018_cs25b095_3_lt),
    .GT(GT), .EQ(EQ), .LT(LT));
endmodule

module cmp16_CS25B018_CS25B095 (
  input  [15:0] A,
  input  [15:0] B,
  output GT,
  output EQ,
  output LT
);

  wire cmp4_cs25b018_cs25b095_1_eq, cmp4_cs25b018_cs25b095_1_gt, cmp4_cs25b018_cs25b095_1_lt,
       cmp4_cs25b018_cs25b095_2_eq, cmp4_cs25b018_cs25b095_2_gt, cmp4_cs25b018_cs25b095_2_lt,
       cmp4_cs25b018_cs25b095_3_eq, cmp4_cs25b018_cs25b095_3_gt, cmp4_cs25b018_cs25b095_3_lt, not_1_out,
       not_2_out, one_bit_comp_helper_cs25b018_cs25b095_1_eq, one_bit_comp_helper_cs25b018_cs25b095_1_gt,
       one_bit_comp_helper_cs25b018_cs25b095_1_lt;

  cmp4_CS25B018_CS25B095 cmp4_cs25b018_cs25b095_1 (
    .A(A[15:12]), .B(B[15:12]), .GTin(one_bit_comp_helper_cs25b018_cs25b095_1_gt),
    .EQin(one_bit_comp_helper_cs25b018_cs25b095_1_eq), .LTin(one_bit_comp_helper_cs25b018_cs25b095_1_lt),
    .GT(cmp4_cs25b018_cs25b095_1_gt), .EQ(cmp4_cs25b018_cs25b095_1_eq), .LT(cmp4_cs25b018_cs25b095_1_lt));
  not not_1 (not_1_out, A[15]);
  not not_2 (not_2_out, B[15]);
  cmp4_CS25B018_CS25B095 cmp4_cs25b018_cs25b095_2 (
    .A(A[11:8]), .B(B[11:8]), .GTin(cmp4_cs25b018_cs25b095_1_gt), .EQin(cmp4_cs25b018_cs25b095_1_eq),
    .LTin(cmp4_cs25b018_cs25b095_1_lt), .GT(cmp4_cs25b018_cs25b095_2_gt), .EQ(cmp4_cs25b018_cs25b095_2_eq),
    .LT(cmp4_cs25b018_cs25b095_2_lt));
  one_bit_comp_helper_CS25B018_CS25B095 one_bit_comp_helper_cs25b018_cs25b095_1 (
    .A(not_1_out), .B(not_2_out), .GTin(1'b0), .EQin(1'b1), .LTin(1'b0),
    .GT(one_bit_comp_helper_cs25b018_cs25b095_1_gt), .EQ(one_bit_comp_helper_cs25b018_cs25b095_1_eq),
    .LT(one_bit_comp_helper_cs25b018_cs25b095_1_lt));
  cmp4_CS25B018_CS25B095 cmp4_cs25b018_cs25b095_3 (
    .A(A[7:4]), .B(B[7:4]), .GTin(cmp4_cs25b018_cs25b095_2_gt), .EQin(cmp4_cs25b018_cs25b095_2_eq),
    .LTin(cmp4_cs25b018_cs25b095_2_lt), .GT(cmp4_cs25b018_cs25b095_3_gt), .EQ(cmp4_cs25b018_cs25b095_3_eq),
    .LT(cmp4_cs25b018_cs25b095_3_lt));
  cmp4_CS25B018_CS25B095 cmp4_cs25b018_cs25b095_4 (
    .A(A[3:0]), .B(B[3:0]), .GTin(cmp4_cs25b018_cs25b095_3_gt), .EQin(cmp4_cs25b018_cs25b095_3_eq),
    .LTin(cmp4_cs25b018_cs25b095_3_lt), .GT(GT), .EQ(EQ), .LT(LT));
endmodule

module logic_unit_CS25B018_CS25B095 (
  input  [15:0] A,
  input  [15:0] B,
  output [15:0] AND_LOGIC,
  output [15:0] OR_LOGIC,
  output [15:0] XOR_LOGIC,
  output [15:0] NOT_LOGIC
);

  assign AND_LOGIC = A & B;  // AND_Gate and_1, 16 bits wide
  assign OR_LOGIC = A | B;  // OR_Gate or_1, 16 bits wide
  assign XOR_LOGIC = A ^ B;  // XOR_Gate xor_1, 16 bits wide
  assign NOT_LOGIC = ~A;  // NOT_Gate not_1, 16 bits wide
endmodule

module alu_CS25B018_CS25B095 (
  input  [4:0] OPCODE,
  input  [15:0] A,
  input  [15:0] B,
  input  ALU_OUTPUT_ENABLE,
  output Z,
  output N,
  output C,
  output V,
  output [15:0] BUS_OUT
);

  wire addsub16_cs25b018_cs25b095_1_cout, addsub16_cs25b018_cs25b095_1_ovf,
       addsub16_cs25b018_cs25b095_2_cout, addsub16_cs25b018_cs25b095_2_ovf, and_1_out, and_2_out, and_3_out,
       and_4_out, cmp16_cs25b018_cs25b095_1_lt, cmp16_cs25b018_cs25b095_2_eq, cmp16_cs25b018_cs25b095_3_eq,
       cmp16_cs25b018_cs25b095_4_eq, cmp16_cs25b018_cs25b095_4_lt, or_1_out, or_2_out;
  wire [15:0] addsub16_cs25b018_cs25b095_1_s, addsub16_cs25b018_cs25b095_2_s, bit_extender_1_out,
       bit_extender_2_out, bit_extender_3_out, logic_unit_cs25b018_cs25b095_1_and_logic,
       logic_unit_cs25b018_cs25b095_1_not_logic, logic_unit_cs25b018_cs25b095_1_or_logic,
       logic_unit_cs25b018_cs25b095_1_xor_logic, multiplexer_1_out, multiplexer_2_out, multiplexer_3_out,
       multiplexer_4_out, multiplexer_5_out, multiplexer_6_out, multiplexer_7_out, multiplexer_8_out,
       multiplexer_9_out, multiplexer_10_out, multiplexer_11_out, multiplexer_12_out, multiplexer_13_out,
       multiplexer_14_out, multiplexer_15_out, multiplexer_16_out, multiplexer_17_out, multiplexer_18_out,
       multiplexer_19_out, multiplexer_20_out, multiplexer_21_out, multiplexer_22_out, multiplexer_23_out,
       multiplexer_24_out, multiplexer_25_out, multiplexer_26_out, multiplexer_27_out, multiplexer_28_out,
       multiplexer_29_out, multiplexer_30_out, multiplexer_31_out, shl16_cs25b018_cs25b095_1_y_16,
       shr16_cs25b018_cs25b095_1_y_16;

  addsub16_CS25B018_CS25B095 addsub16_cs25b018_cs25b095_1 (
    .A(A), .B(B), .SUB(1'b0), .S(addsub16_cs25b018_cs25b095_1_s), .COUT(addsub16_cs25b018_cs25b095_1_cout),
    .OVF(addsub16_cs25b018_cs25b095_1_ovf));
  addsub16_CS25B018_CS25B095 addsub16_cs25b018_cs25b095_2 (
    .A(A), .B(B), .SUB(1'b1), .S(addsub16_cs25b018_cs25b095_2_s), .COUT(addsub16_cs25b018_cs25b095_2_cout),
    .OVF(addsub16_cs25b018_cs25b095_2_ovf));
  logic_unit_CS25B018_CS25B095 logic_unit_cs25b018_cs25b095_1 (
    .A(A), .B(B), .AND_LOGIC(logic_unit_cs25b018_cs25b095_1_and_logic),
    .OR_LOGIC(logic_unit_cs25b018_cs25b095_1_or_logic), .XOR_LOGIC(logic_unit_cs25b018_cs25b095_1_xor_logic),
    .NOT_LOGIC(logic_unit_cs25b018_cs25b095_1_not_logic));
  shl16_CS25B018_CS25B095 shl16_cs25b018_cs25b095_1 (.A(A), .SHL_5(B[4:0]), .Y_16(shl16_cs25b018_cs25b095_1_y_16));
  shr16_CS25B018_CS25B095 shr16_cs25b018_cs25b095_1 (.A(A), .SHR_5(B[4:0]), .Y_16(shr16_cs25b018_cs25b095_1_y_16));
  cmp16_CS25B018_CS25B095 cmp16_cs25b018_cs25b095_1 (.A(A), .B(B), .LT(cmp16_cs25b018_cs25b095_1_lt));  // open: GT, EQ
  assign bit_extender_1_out = {{15{1'b0}}, cmp16_cs25b018_cs25b095_1_lt};  // Bit_Extender bit_extender_1
  assign bit_extender_2_out = {{11{1'b0}}, OPCODE};  // Bit_Extender bit_extender_2
  assign bit_extender_3_out = {{11{1'b0}}, OPCODE};  // Bit_Extender bit_extender_3
  Multiplexer #(.width(16)) multiplexer_1 (
    .in0({16{1'b0}}), .in1({16{1'b0}}), .out(multiplexer_1_out), .sel(OPCODE[0]));
  Multiplexer #(.width(16)) multiplexer_2 (
    .in0({16{1'b0}}), .in1({16{1'b0}}), .out(multiplexer_2_out), .sel(OPCODE[0]));
  Multiplexer #(.width(16)) multiplexer_3 (
    .in0({16{1'b0}}), .in1({16{1'b0}}), .out(multiplexer_3_out), .sel(OPCODE[0]));
  Multiplexer #(.width(16)) multiplexer_4 (
    .in0({16{1'b0}}), .in1({16{1'b0}}), .out(multiplexer_4_out), .sel(OPCODE[0]));
  Multiplexer #(.width(16)) multiplexer_5 (
    .in0({16{1'b0}}), .in1(addsub16_cs25b018_cs25b095_1_s), .out(multiplexer_5_out), .sel(OPCODE[0]));
  Multiplexer #(.width(16)) multiplexer_6 (
    .in0(addsub16_cs25b018_cs25b095_2_s), .in1({16{1'b0}}), .out(multiplexer_6_out), .sel(OPCODE[0]));
  Multiplexer #(.width(16)) multiplexer_7 (
    .in0({16{1'b0}}), .in1(logic_unit_cs25b018_cs25b095_1_and_logic), .out(multiplexer_7_out), .sel(OPCODE[0]));
  Multiplexer #(.width(16)) multiplexer_8 (
    .in0(logic_unit_cs25b018_cs25b095_1_or_logic), .in1(logic_unit_cs25b018_cs25b095_1_xor_logic),
    .out(multiplexer_8_out), .sel(OPCODE[0]));
  Multiplexer #(.width(16)) multiplexer_9 (
    .in0(logic_unit_cs25b018_cs25b095_1_not_logic), .in1(shl16_cs25b018_cs25b095_1_y_16),
    .out(multiplexer_9_out), .sel(OPCODE[0]));
  Multiplexer #(.width(16)) multiplexer_10 (
    .in0(shr16_cs25b018_cs25b095_1_y_16), .in1(bit_extender_1_out), .out(multiplexer_10_out), .sel(OPCODE[0]));
  Multiplexer #(.width(16)) multiplexer_11 (
    .in0({16{1'b0}}), .in1({16{1'b0}}), .out(multiplexer_11_out), .sel(OPCODE[0]));
  Multiplexer #(.width(16)) multiplexer_12 (
    .in0({16{1'b0}}), .in1({16{1'b0}}), .out(multiplexer_12_out), .sel(OPCODE[0]));
  Multiplexer #(.width(16)) multiplexer_13 (
    .in0({16{1'b0}}), .in1({16{1'b0}}), .out(multiplexer_13_out), .sel(OPCODE[0]));
  Multiplexer #(.width(16)) multiplexer_14 (
    .in0({16{1'b0}}), .in1({16{1'b0}}), .out(multiplexer_14_out), .sel(OPCODE[0]));
  Multiplexer #(.width(16)) multiplexer_15 (
    .in0({16{1'b0}}), .in1({16{1'b0}}), .out(multiplexer_15_out), .sel(OPCODE[0]));
  Multiplexer #(.width(16)) multiplexer_16 (
    .in0({16{1'b0}}), .in1({16{1'b0}}), .out(multiplexer_16_out), .sel(OPCODE[0]));
  Multiplexer #(.width(16)) multiplexer_17 (
    .in0(multiplexer_1_out), .in1(multiplexer_2_out), .out(multiplexer_17_out), .sel(OPCODE[1]));
  Multiplexer #(.width(16)) multiplexer_18 (
    .in0(multiplexer_3_out), .in1(multiplexer_4_out), .out(multiplexer_18_out), .sel(OPCODE[1]));
  Multiplexer #(.width(16)) multiplexer_19 (
    .in0(multiplexer_5_out), .in1(multiplexer_6_out), .out(multiplexer_19_out), .sel(OPCODE[1]));
  Multiplexer #(.width(16)) multiplexer_20 (
    .in0(multiplexer_7_out), .in1(multiplexer_8_out), .out(multiplexer_20_out), .sel(OPCODE[1]));
  Multiplexer #(.width(16)) multiplexer_21 (
    .in0(multiplexer_9_out), .in1(multiplexer_10_out), .out(multiplexer_21_out), .sel(OPCODE[1]));
  Multiplexer #(.width(16)) multiplexer_22 (
    .in0(multiplexer_11_out), .in1(multiplexer_12_out), .out(multiplexer_22_out), .sel(OPCODE[1]));
  Multiplexer #(.width(16)) multiplexer_23 (
    .in0(multiplexer_13_out), .in1(multiplexer_14_out), .out(multiplexer_23_out), .sel(OPCODE[1]));
  Multiplexer #(.width(16)) multiplexer_24 (
    .in0(multiplexer_15_out), .in1(multiplexer_16_out), .out(multiplexer_24_out), .sel(OPCODE[1]));
  Multiplexer #(.width(16)) multiplexer_25 (
    .in0(multiplexer_17_out), .in1(multiplexer_18_out), .out(multiplexer_25_out), .sel(OPCODE[2]));
  Multiplexer #(.width(16)) multiplexer_26 (
    .in0(multiplexer_19_out), .in1(multiplexer_20_out), .out(multiplexer_26_out), .sel(OPCODE[2]));
  Multiplexer #(.width(16)) multiplexer_27 (
    .in0(multiplexer_21_out), .in1(multiplexer_22_out), .out(multiplexer_27_out), .sel(OPCODE[2]));
  Multiplexer #(.width(16)) multiplexer_28 (
    .in0(multiplexer_23_out), .in1(multiplexer_24_out), .out(multiplexer_28_out), .sel(OPCODE[2]));
  Multiplexer #(.width(16)) multiplexer_29 (
    .in0(multiplexer_25_out), .in1(multiplexer_26_out), .out(multiplexer_29_out), .sel(OPCODE[3]));
  Multiplexer #(.width(16)) multiplexer_30 (
    .in0(multiplexer_27_out), .in1(multiplexer_28_out), .out(multiplexer_30_out), .sel(OPCODE[3]));
  cmp16_CS25B018_CS25B095 cmp16_cs25b018_cs25b095_2 (
    .A(16'h9), .B(bit_extender_2_out), .EQ(cmp16_cs25b018_cs25b095_2_eq));  // open: GT, LT
  Multiplexer #(.width(16)) multiplexer_31 (
    .in0(multiplexer_29_out), .in1(multiplexer_30_out), .out(multiplexer_31_out), .sel(OPCODE[4]));
  assign BUS_OUT = ALU_OUTPUT_ENABLE ? multiplexer_31_out : 16'bz;  // Controlled_Buffer controlled_buffer_1
  cmp16_CS25B018_CS25B095 cmp16_cs25b018_cs25b095_3 (
    .A(16'ha), .B(bit_extender_3_out), .EQ(cmp16_cs25b018_cs25b095_3_eq));  // open: GT, LT
  and and_1 (and_1_out, cmp16_cs25b018_cs25b095_3_eq, addsub16_cs25b018_cs25b095_2_cout);
  and and_2 (and_2_out, cmp16_cs25b018_cs25b095_3_eq, addsub16_cs25b018_cs25b095_2_ovf);
  and and_3 (and_3_out, cmp16_cs25b018_cs25b095_2_eq, addsub16_cs25b018_cs25b095_1_cout);
  and and_4 (and_4_out, cmp16_cs25b018_cs25b095_2_eq, addsub16_cs25b018_cs25b095_1_ovf);
  cmp16_CS25B018_CS25B095 cmp16_cs25b018_cs25b095_4 (
    .A(multiplexer_31_out), .B({16{1'b0}}), .EQ(cmp16_cs25b018_cs25b095_4_eq),
    .LT(cmp16_cs25b018_cs25b095_4_lt));  // open: GT
  or or_1 (or_1_out, and_1_out, and_3_out);
  or or_2 (or_2_out, and_2_out, and_4_out);
  assign C = ALU_OUTPUT_ENABLE ? or_1_out : 1'bz;  // Controlled_Buffer controlled_buffer_2
  assign V = ALU_OUTPUT_ENABLE ? or_2_out : 1'bz;  // Controlled_Buffer controlled_buffer_3
  assign Z = ALU_OUTPUT_ENABLE ? cmp16_cs25b018_cs25b095_4_eq : 1'bz;  // Controlled_Buffer controlled_buffer_4
  assign N = ALU_OUTPUT_ENABLE ? cmp16_cs25b018_cs25b095_4_lt : 1'bz;  // Controlled_Buffer controlled_buffer_5

  // Notes on the sheet:
  //   op_9
  //   op_10
  //   op_13-16
  //   op_17
  //   op_18
  //   op_19
  //   op_20-32
  //   0-1
  //   2-3
  //   4-5
  //   6-7
  //   8-9
  //   10-11
  //   12-13
  //   14-15
  //   16-17
  //   18-19
  //   20-21
  //   22-23
  //   24-25
  //   26-27
  //   28-29
  //   30-31
  //   0-3
  //   4-7
  //   8-11
  //   12-15
  //   16-19
  //   24-27
  //   28-31
  //   20-23
  //   0-7
  //   8-15
endmodule

module tara_decoder_CS25B018_CS25B095 (
  input  [15:0] IR,
  output [4:0] OPCODE,
  output [2:0] FORMAT,
  output [10:0] REL11,
  output [2:0] RD,
  output [7:0] IMMA8,
  output [7:0] REL8,
  output [2:0] RA,
  output [4:0] OFF5,
  output [2:0] RB
);

  Multiplexer #(.select(5), .width(3)) multiplexer_1 (
    .in0(3'b000), .in1(3'b000), .in2(3'b010), .in3(3'b011), .in4(3'b011), .in5(3'b100), .in6(3'b100),
    .in7(3'b100), .in8(3'b100), .in9(3'b001), .in10(3'b001), .in11(3'b011), .in12(3'b001), .in13(3'b001),
    .in14(3'b001), .in15(3'b001), .in16(3'b010), .in17(3'b011), .in18(3'b011), .in19(3'b001), .in20(3'b101),
    .in21(3'b101), .in22(3'b110), .in23(3'b110), .in24(3'b000), .in25(3'b111), .in26(3'b111), .out(FORMAT),
    .sel(IR[15:11]));  // open: in27, in28, in29, in30, in31

  assign IMMA8 = IR[7:0];
  assign OFF5 = IR[4:0];
  assign OPCODE = IR[15:11];
  assign RA = IR[7:5];
  assign RB = IR[4:2];
  assign RD = IR[10:8];
  assign REL8 = IR[7:0];
  assign REL11 = IR[10:0];
endmodule

module tara_datapath_CS25B018_CS25B095 (
  input  [2:0] BUS_SOURCE,
  input  CLK,
  input  MAR_LOAD,
  input  PC_LOAD,
  input  PC_FETCH_EN,
  input  PC_RST,
  input  MEM_WRITE,
  input  MEM_READ,
  input  MDR_LOAD,
  input  [2:0] REG_A,
  input  [2:0] REG_B,
  input  [2:0] REG_D,
  input  REG_WE,
  input  IR_LOAD,
  input  REG_RST,
  input  [7:0] IMM8,
  input  [4:0] IMM5,
  input  [1:0] IMM_BIT_EXTEND,
  input  [4:0] OPCODE,
  input  STATUS_WE,
  input  ACC_LOAD,
  output [15:0] MAR_OUT,
  output [15:0] RAM_WORD_OUT,
  output [15:0] R0,
  output [15:0] R1,
  output [15:0] R2,
  output [15:0] R3,
  output [15:0] R4,
  output [15:0] R5,
  output [15:0] R6,
  output [15:0] R7,
  output Z_OUT,
  output N_OUT,
  output C_OUT,
  output V_OUT,
  output [15:0] ALU_OUT,
  output [15:0] ACC_OUT,
  output [15:0] PC_OUT,
  output [15:0] MDR_OUT,
  output [15:0] IR_OUT,
  output [15:0] IMM_OUT,
  output [15:0] BUS_VALUE
);

  wire alu_cs25b018_cs25b095_1_c, alu_cs25b018_cs25b095_1_n, alu_cs25b018_cs25b095_1_v,
       alu_cs25b018_cs25b095_1_z, decoder_1_out0, decoder_1_out1, decoder_1_out2, decoder_1_out3,
       decoder_1_out4, decoder_1_out5, decoder_1_out6, not_1_out;
  wire [15:0] regfile8x16_cs25b018_cs25b095_1_qa, regfile8x16_cs25b018_cs25b095_1_qb;

  Decoder #(.select(3)) decoder_1 (
    .out0(decoder_1_out0), .out1(decoder_1_out1), .out2(decoder_1_out2), .out3(decoder_1_out3),
    .out4(decoder_1_out4), .out5(decoder_1_out5), .out6(decoder_1_out6), .sel(BUS_SOURCE), .en(1'b1));  // open: out7
  PC_CS25B018_CS25B095 pc_cs25b018_cs25b095_1 (
    .FETCH(BUS_VALUE), .CLK(CLK), .PC_LOAD(PC_LOAD), .FETCH_EN(PC_FETCH_EN), .RST(PC_RST), .P_C(PC_OUT));
  MDR_CS25B018_CS25B095 mdr_cs25b018_cs25b095_1 (
    .MDR_IN(BUS_VALUE), .CLK(CLK), .MDR_LOAD(MDR_LOAD), .MDR_OUT(MDR_OUT));  // open: RST
  IR_CS25B018_CS25B095 ir_cs25b018_cs25b095_1 (
    .MDR_OUT(BUS_VALUE), .CLK(CLK), .IR_LOAD(IR_LOAD), .IR_OUT(IR_OUT));  // open: RST
  IMM_CS25B018_CS25B095 imm_cs25b018_cs25b095_1 (
    .IMM8(IMM8), .IMM5(IMM5), .BIT_EXTEND(IMM_BIT_EXTEND), .IMM_OUT(IMM_OUT));
  assign BUS_VALUE = decoder_1_out0 ? PC_OUT : 16'bz;  // Controlled_Buffer controlled_buffer_1
  assign BUS_VALUE = decoder_1_out1 ? MDR_OUT : 16'bz;  // Controlled_Buffer controlled_buffer_2
  assign BUS_VALUE = decoder_1_out2 ? IR_OUT : 16'bz;  // Controlled_Buffer controlled_buffer_3
  assign BUS_VALUE = decoder_1_out4 ? regfile8x16_cs25b018_cs25b095_1_qa : 16'bz;  // Controlled_Buffer controlled_buffer_4
  assign BUS_VALUE = decoder_1_out3 ? IMM_OUT : 16'bz;  // Controlled_Buffer controlled_buffer_5
  assign BUS_VALUE = decoder_1_out5 ? ACC_OUT : 16'bz;  // Controlled_Buffer controlled_buffer_6
  assign BUS_VALUE = decoder_1_out6 ? RAM_WORD_OUT : 16'bz;  // Controlled_Buffer controlled_buffer_7
  not not_1 (not_1_out, CLK);
  MAR_CS25B018_CS25B095 mar_cs25b018_cs25b095_1 (
    .MAR_IN(BUS_VALUE), .CLK(CLK), .MAR_LOAD(MAR_LOAD), .MAR_OP(MAR_OUT));  // open: RST
  ram_word_CS25B018_CS25B095 ram_word_cs25b018_cs25b095_1 (
    .ADDR(MAR_OUT), .DIN(MDR_OUT), .MEM_WRITE(MEM_WRITE), .MEM_READ(MEM_READ), .CLK(not_1_out),
    .DOUT(RAM_WORD_OUT));
  regfile8x16_CS25B018_CS25B095 regfile8x16_cs25b018_cs25b095_1 (
    .RA(REG_A), .RB(REG_B), .RD(REG_D), .D(BUS_VALUE), .WE(REG_WE), .CLK(CLK), .RST(REG_RST),
    .QA(regfile8x16_cs25b018_cs25b095_1_qa), .QB(regfile8x16_cs25b018_cs25b095_1_qb), .R0(R0), .R1(R1),
    .R2(R2), .R3(R3), .R4(R4), .R5(R5), .R6(R6), .R7(R7));
  alu_CS25B018_CS25B095 alu_cs25b018_cs25b095_1 (
    .OPCODE(OPCODE), .A(regfile8x16_cs25b018_cs25b095_1_qb), .B(BUS_VALUE), .ALU_OUTPUT_ENABLE(1'b1),
    .Z(alu_cs25b018_cs25b095_1_z), .N(alu_cs25b018_cs25b095_1_n), .C(alu_cs25b018_cs25b095_1_c),
    .V(alu_cs25b018_cs25b095_1_v), .BUS_OUT(ALU_OUT));
  register16_CS25B018_CS25B095 ACC (.D(ALU_OUT), .CLK(CLK), .LOAD(ACC_LOAD), .Q(ACC_OUT));  // open: RST
  status_reg_CS25B018_CS25B095 status_reg_cs25b018_cs25b095_1 (
    .Z_IN(alu_cs25b018_cs25b095_1_z), .N_IN(alu_cs25b018_cs25b095_1_n), .C_IN(alu_cs25b018_cs25b095_1_c),
    .V_IN(alu_cs25b018_cs25b095_1_v), .STATUS_WE(STATUS_WE), .CLK(CLK), .Z(Z_OUT), .N(N_OUT), .C(C_OUT),
    .V(V_OUT));  // open: RST

  // Notes on the sheet:
  //   BUS_SOURCE INPUT:
  //   000 - PC Read
  //   001 - MDR Read
  //   010 - IR Read
  //   011 - IMM Read
  //   101 - ACC Read
  //   111 - BUS Off
  //   100 - RegFile Read
  //   110 - RamWord Read
endmodule

module IMM_CS25B018_CS25B095 (
  input  [7:0] IMM8,
  input  [4:0] IMM5,
  input  [1:0] BIT_EXTEND,
  output [15:0] IMM_OUT
);

  wire [15:0] bit_extender_1_out, bit_extender_2_out, bit_extender_3_out;

  assign bit_extender_1_out = {{8{1'b0}}, IMM8};  // Bit_Extender bit_extender_1
  assign bit_extender_2_out = {{8{IMM8[7]}}, IMM8};  // Bit_Extender bit_extender_2
  assign bit_extender_3_out = {{11{1'b0}}, IMM5};  // Bit_Extender bit_extender_3
  Multiplexer #(.select(2), .width(16)) multiplexer_1 (
    .in0(bit_extender_1_out), .in1(bit_extender_2_out), .in2({IMM8, {8{1'b0}}}), .in3(bit_extender_3_out),
    .out(IMM_OUT), .sel(BIT_EXTEND));

  // Notes on the sheet:
  //   BIT_EXTEND Input:
  //   00 - 0 extend 15-8 bits
  //   01 - sign extend 15-8 bits
  //   10 - 0 extend 0-7 bits
  //   11 - imm5 extend
endmodule

module tstate_counter_CS25B018_CS25B095 (
  input  STEP_RESET,
  input  TSTATE_HALT,
  input  CLK,
  input  RST,
  output [3:0] TSTATE
);

  wire not_1_out;
  wire [3:0] adder_1_out, multiplexer_1_out;

  Multiplexer #(.width(4)) multiplexer_1 (.in0(adder_1_out), .in1(4'b0000), .out(multiplexer_1_out), .sel(STEP_RESET));
  not not_1 (not_1_out, TSTATE_HALT);
  Register #(.width(4)) register_1 (.D(multiplexer_1_out), .en(not_1_out), .clk(CLK), .Q(TSTATE), .clr(RST));
  Adder #(.width(4)) adder_1 (.a(4'b0001), .b(TSTATE), .out(adder_1_out));  // open: cin, cout
endmodule

module ROM_ADDRESS_CS25B018_CS25B095 (
  input  Z,
  input  N,
  input  [4:0] OPCODE,
  input  [3:0] TSTATE_OUT,
  output [10:0] ROM_ADDR
);


  assign ROM_ADDR = {Z, N, OPCODE, TSTATE_OUT};
endmodule

module control_rom_CS25B018_CS25B095 (
  input  [10:0] ROM_ADDR,
  output [24:0] CONTROL
);

  ROM #(.addrWidth(11), .dataWidth(25)) ROM_DATA (.addr(ROM_ADDR), .data(CONTROL));

  // Notes on the sheet:
  //   contents of ROM_DATA (hex, n*v repeats v):
  //   2 1c0044 20008 13*e0001 2 1c0044 20008 4e0000 12*e0001 2 1c0044 20008 69c10 a0021 11*e0001 2 1c0044
  //   20008 60021 12*e0001 2 1c0044 20008 6d210 a0020 6e810 a0021 9*e0001 2 1c0044 20008 13*e0001 2 1c0044
  //   20008 13*e0001 2 1c0044 20008 13*e0001 2 1c0044 20008 13*e0001 2 1c0044 20008 89010 a0021 11*e0001 2
  //   1c0044 20008 8a010 a0021 11*e0001 2 1c0044 20008 69410 a0021 11*e0001 2 1c0044 20008 13*e0001 2
  //   1c0044 20008 8d010 a0021 11*e0001 2 1c0044 20008 8e010 a0021 11*e0001 2 1c0044 20008 8f010 a0021
  //   11*e0001 2 1c0044 20008 90010 a0021 11*e0001 2 1c0044 20008 71c10 a0021 11*e0001 2 1c0044 20008
  //   72c10 a0021 11*e0001 2 1c0044 20008 93010 a0021 11*e0001 2 1c0044 20008 13*e0001 2 1c0044 20008
  //   13*e0001 2 1c0044 20008 13*e0001 2 1c0044 20008 13*e0001 2 1c0044 20008 13*e0001 2 1c0044 20008
  //   13*e0001 2 1c0044 20008 13*e0001 2 1c0044 20008 13*e0001 2 1c0044 20008 13*e0001 2 1c0044 20008
  //   13*e0001 2 1c0044 20008 13*e0001 2 1c0044 20008 13*e0001 2 1c0044 20008 13*e0001 2 1c0044 20008
  //   4e0000 12*e0001 2 1c0044 20008 69c10 a0021 11*e0001 2 1c0044 20008 60021 12*e0001 2 1c0044 20008
  //   6d210 a0020 6e810 a0021 9*e0001 2 1c0044 20008 13*e0001 2 1c0044 20008 13*e0001 2 1c0044 20008
  //   13*e0001 2 1c0044 20008 13*e0001 2 1c0044 20008 89010 a0021 11*e0001 2 1c0044 20008 8a010 a0021
  //   11*e0001 2 1c0044 20008 69410 a0021 11*e0001 2 1c0044 20008 13*e0001 2 1c0044 20008 8d010 a0021
  //   11*e0001 2 1c0044 20008 8e010 a0021 11*e0001 2 1c0044 20008 8f010 a0021 11*e0001 2 1c0044 20008
  //   90010 a0021 11*e0001 2 1c0044 20008 71c10 a0021 11*e0001 2 1c0044 20008 72c10 a0021 11*e0001 2
  //   1c0044 20008 93010 a0021 11*e0001 2 1c0044 20008 13*e0001 2 1c0044 20008 13*e0001 2 1c0044 20008
  //   13*e0001 2 1c0044 20008 13*e0001 2 1c0044 20008 13*e0001 2 1c0044 20008 13*e0001 2 1c0044 20008
  //   13*e0001 2 1c0044 20008 13*e0001 2 1c0044 20008 13*e0001 2 1c0044 20008 13*e0001 2 1c0044 20008
  //   13*e0001 2 1c0044 20008 13*e0001 2 1c0044 20008 13*e0001 2 1c0044 20008 4e0000 12*e0001 2 1c0044
  //   20008 69c10 a0021 11*e0001 2 1c0044 20008 60021 12*e0001 2 1c0044 20008 6d210 a0020 6e810 a0021
  //   9*e0001 2 1c0044 20008 13*e0001 2 1c0044 20008 13*e0001 2 1c0044 20008 13*e0001 2 1c0044 20008
  //   13*e0001 2 1c0044 20008 89010 a0021 11*e0001 2 1c0044 20008 8a010 a0021 11*e0001 2 1c0044 20008
  //   69410 a0021 11*e0001 2 1c0044 20008 13*e0001 2 1c0044 20008 8d010 a0021 11*e0001 2 1c0044 20008
  //   8e010 a0021 11*e0001 2 1c0044 20008 8f010 a0021 11*e0001 2 1c0044 20008 90010 a0021 11*e0001 2
  //   1c0044 20008 71c10 a0021 11*e0001 2 1c0044 20008 72c10 a0021 11*e0001 2 1c0044 20008 93010 a0021
  //   11*e0001 2 1c0044 20008 13*e0001 2 1c0044 20008 13*e0001 2 1c0044 20008 13*e0001 2 1c0044 20008
  //   13*e0001 2 1c0044 20008 13*e0001 2 1c0044 20008 13*e0001 2 1c0044 20008 13*e0001 2 1c0044 20008
  //   13*e0001 2 1c0044 20008 13*e0001 2 1c0044 20008 13*e0001 2 1c0044 20008 13*e0001 2 1c0044 20008
  //   13*e0001 2 1c0044 20008 13*e0001 2 1c0044 20008 4e0000 12*e0001 2 1c0044 20008 69c10 a0021 11*e0001
  //   2 1c0044 20008 60021 12*e0001 2 1c0044 20008 6d210 a0020 6e810 a0021 9*e0001 2 1c0044 20008 13*e0001
  //   2 1c0044 20008 13*e0001 2 1c0044 20008 13*e0001 2 1c0044 20008 13*e0001 2 1c0044 20008 89010 a0021
  //   11*e0001 2 1c0044 20008 8a010 a0021 11*e0001 2 1c0044 20008 69410 a0021 11*e0001 2 1c0044 20008
  //   13*e0001 2 1c0044 20008 8d010 a0021 11*e0001 2 1c0044 20008 8e010 a0021 11*e0001 2 1c0044 20008
  //   8f010 a0021 11*e0001 2 1c0044 20008 90010 a0021 11*e0001 2 1c0044 20008 71c10 a0021 11*e0001 2
  //   1c0044 20008 72c10 a0021 11*e0001 2 1c0044 20008 93010 a0021 11*e0001 2 1c0044 20008 13*e0001 2
  //   1c0044 20008 13*e0001 2 1c0044 20008 13*e0001 2 1c0044 20008 13*e0001 2 1c0044 20008 13*e0001 2
  //   1c0044 20008 13*e0001 2 1c0044 20008 13*e0001 2 1c0044 20008 13*e0001 2 1c0044 20008 13*e0001 2
  //   1c0044 20008 13*e0001 2 1c0044 20008 13*e0001 2 1c0044 20008 13*e0001
endmodule

module tara_control_CS25B018_CS25B095 (
  input  Z,
  input  N,
  input  [4:0] OPCODE,
  input  [3:0] TSTATE_OUT,
  output STEP_RST,
  output MAR_LOAD,
  output MDR_LOAD,
  output IR_LOAD,
  output ACC_LOAD,
  output REG_WE,
  output MEM_READ,
  output MEM_WRITE,
  output STATUS_WE,
  output IMM,
  output [1:0] IMM_BIT_EXTEND,
  output [4:0] ALU_OPCODE,
  output [2:0] BUS_SOURCE,
  output PC_LOAD,
  output PC_FETCH_EN,
  output HALT,
  output SPARE_1,
  output SPARE_2
);

  wire [10:0] rom_address_cs25b018_cs25b095_1_rom_addr;

  ROM_ADDRESS_CS25B018_CS25B095 rom_address_cs25b018_cs25b095_1 (
    .Z(Z), .N(N), .OPCODE(OPCODE), .TSTATE_OUT(TSTATE_OUT),
    .ROM_ADDR(rom_address_cs25b018_cs25b095_1_rom_addr));
  control_rom_CS25B018_CS25B095 control_rom_cs25b018_cs25b095_1 (
    .ROM_ADDR(rom_address_cs25b018_cs25b095_1_rom_addr),
    .CONTROL({SPARE_2, SPARE_1, HALT, PC_FETCH_EN, PC_LOAD, BUS_SOURCE, ALU_OPCODE, IMM_BIT_EXTEND, IMM, STATUS_WE, MEM_WRITE, MEM_READ, REG_WE, ACC_LOAD, IR_LOAD, MDR_LOAD, MAR_LOAD, STEP_RST}));
endmodule

module tara_cpu_CS25B018_CS25B095 (
  input  CLK,
  input  RST,
  output [3:0] TSTATE,
  output [15:0] PC_COUNT,
  output [15:0] RAM_WORD,
  output [15:0] MAR_OUT,
  output [15:0] MDR_OUT,
  output [15:0] IR_OUT,
  output [15:0] R0,
  output [15:0] R1,
  output [15:0] R2,
  output [15:0] R3,
  output [15:0] R4,
  output [15:0] R5,
  output [15:0] R6,
  output [15:0] R7
);

  wire comparator_1_eq, tara_control_cs25b018_cs25b095_1_acc_load, tara_control_cs25b018_cs25b095_1_halt,
       tara_control_cs25b018_cs25b095_1_imm, tara_control_cs25b018_cs25b095_1_ir_load,
       tara_control_cs25b018_cs25b095_1_mar_load, tara_control_cs25b018_cs25b095_1_mdr_load,
       tara_control_cs25b018_cs25b095_1_mem_read, tara_control_cs25b018_cs25b095_1_mem_write,
       tara_control_cs25b018_cs25b095_1_pc_fetch_en, tara_control_cs25b018_cs25b095_1_pc_load,
       tara_control_cs25b018_cs25b095_1_reg_we, tara_control_cs25b018_cs25b095_1_status_we,
       tara_control_cs25b018_cs25b095_1_step_rst, tara_datapath_cs25b018_cs25b095_1_n_out,
       tara_datapath_cs25b018_cs25b095_1_z_out;
  wire [1:0] tara_control_cs25b018_cs25b095_1_imm_bit_extend;
  wire [2:0] multiplexer_1_out, multiplexer_2_out, tara_control_cs25b018_cs25b095_1_bus_source,
       tara_decoder_cs25b018_cs25b095_1_format, tara_decoder_cs25b018_cs25b095_1_ra,
       tara_decoder_cs25b018_cs25b095_1_rb, tara_decoder_cs25b018_cs25b095_1_rd;
  wire [4:0] tara_control_cs25b018_cs25b095_1_alu_opcode, tara_decoder_cs25b018_cs25b095_1_off5,
       tara_decoder_cs25b018_cs25b095_1_opcode;
  wire [7:0] multiplexer_3_out, tara_decoder_cs25b018_cs25b095_1_imma8;

  tstate_counter_CS25B018_CS25B095 tstate_counter_cs25b018_cs25b095_1 (
    .STEP_RESET(tara_control_cs25b018_cs25b095_1_step_rst),
    .TSTATE_HALT(tara_control_cs25b018_cs25b095_1_halt), .CLK(CLK), .RST(RST), .TSTATE(TSTATE));
  tara_control_CS25B018_CS25B095 tara_control_cs25b018_cs25b095_1 (
    .Z(tara_datapath_cs25b018_cs25b095_1_z_out), .N(tara_datapath_cs25b018_cs25b095_1_n_out),
    .OPCODE(tara_decoder_cs25b018_cs25b095_1_opcode), .TSTATE_OUT(TSTATE),
    .STEP_RST(tara_control_cs25b018_cs25b095_1_step_rst),
    .MAR_LOAD(tara_control_cs25b018_cs25b095_1_mar_load),
    .MDR_LOAD(tara_control_cs25b018_cs25b095_1_mdr_load), .IR_LOAD(tara_control_cs25b018_cs25b095_1_ir_load),
    .ACC_LOAD(tara_control_cs25b018_cs25b095_1_acc_load), .REG_WE(tara_control_cs25b018_cs25b095_1_reg_we),
    .MEM_READ(tara_control_cs25b018_cs25b095_1_mem_read),
    .MEM_WRITE(tara_control_cs25b018_cs25b095_1_mem_write),
    .STATUS_WE(tara_control_cs25b018_cs25b095_1_status_we), .IMM(tara_control_cs25b018_cs25b095_1_imm),
    .IMM_BIT_EXTEND(tara_control_cs25b018_cs25b095_1_imm_bit_extend),
    .ALU_OPCODE(tara_control_cs25b018_cs25b095_1_alu_opcode),
    .BUS_SOURCE(tara_control_cs25b018_cs25b095_1_bus_source),
    .PC_LOAD(tara_control_cs25b018_cs25b095_1_pc_load),
    .PC_FETCH_EN(tara_control_cs25b018_cs25b095_1_pc_fetch_en), .HALT(tara_control_cs25b018_cs25b095_1_halt));  // open: SPARE_1, SPARE_2
  tara_datapath_CS25B018_CS25B095 tara_datapath_cs25b018_cs25b095_1 (
    .BUS_SOURCE(tara_control_cs25b018_cs25b095_1_bus_source), .CLK(CLK),
    .MAR_LOAD(tara_control_cs25b018_cs25b095_1_mar_load), .PC_LOAD(tara_control_cs25b018_cs25b095_1_pc_load),
    .PC_FETCH_EN(tara_control_cs25b018_cs25b095_1_pc_fetch_en), .PC_RST(RST),
    .MEM_WRITE(tara_control_cs25b018_cs25b095_1_mem_write),
    .MEM_READ(tara_control_cs25b018_cs25b095_1_mem_read),
    .MDR_LOAD(tara_control_cs25b018_cs25b095_1_mdr_load), .REG_A(multiplexer_2_out),
    .REG_B(multiplexer_1_out), .REG_D(tara_decoder_cs25b018_cs25b095_1_rd),
    .REG_WE(tara_control_cs25b018_cs25b095_1_reg_we), .IR_LOAD(tara_control_cs25b018_cs25b095_1_ir_load),
    .REG_RST(RST), .IMM8(multiplexer_3_out), .IMM5(tara_decoder_cs25b018_cs25b095_1_off5),
    .IMM_BIT_EXTEND(tara_control_cs25b018_cs25b095_1_imm_bit_extend),
    .OPCODE(tara_control_cs25b018_cs25b095_1_alu_opcode),
    .STATUS_WE(tara_control_cs25b018_cs25b095_1_status_we),
    .ACC_LOAD(tara_control_cs25b018_cs25b095_1_acc_load), .MAR_OUT(MAR_OUT), .RAM_WORD_OUT(RAM_WORD),
    .R0(R0), .R1(R1), .R2(R2), .R3(R3), .R4(R4), .R5(R5), .R6(R6), .R7(R7),
    .Z_OUT(tara_datapath_cs25b018_cs25b095_1_z_out), .N_OUT(tara_datapath_cs25b018_cs25b095_1_n_out),
    .PC_OUT(PC_COUNT), .MDR_OUT(MDR_OUT), .IR_OUT(IR_OUT));  // open: C_OUT, V_OUT, ALU_OUT, ACC_OUT, IMM_OUT, BUS_VALUE
  tara_decoder_CS25B018_CS25B095 tara_decoder_cs25b018_cs25b095_1 (
    .IR(IR_OUT), .OPCODE(tara_decoder_cs25b018_cs25b095_1_opcode),
    .FORMAT(tara_decoder_cs25b018_cs25b095_1_format), .RD(tara_decoder_cs25b018_cs25b095_1_rd),
    .IMMA8(tara_decoder_cs25b018_cs25b095_1_imma8), .RA(tara_decoder_cs25b018_cs25b095_1_ra),
    .OFF5(tara_decoder_cs25b018_cs25b095_1_off5), .RB(tara_decoder_cs25b018_cs25b095_1_rb));  // open: REL11, REL8
  Comparator #(.mode("unsigned"), .width(3)) comparator_1 (
    .a(3'b011), .b(tara_decoder_cs25b018_cs25b095_1_format), .eq(comparator_1_eq));  // open: gt, lt
  Multiplexer #(.width(3)) multiplexer_1 (
    .in0(tara_decoder_cs25b018_cs25b095_1_ra), .in1(tara_decoder_cs25b018_cs25b095_1_rd),
    .out(multiplexer_1_out), .sel(comparator_1_eq));
  Multiplexer #(.width(3)) multiplexer_2 (
    .in0(tara_decoder_cs25b018_cs25b095_1_rb), .in1(tara_decoder_cs25b018_cs25b095_1_rd),
    .out(multiplexer_2_out), .sel(comparator_1_eq));
  Multiplexer #(.width(8)) multiplexer_3 (
    .in0(tara_decoder_cs25b018_cs25b095_1_imma8), .in1({8{1'b1}}), .out(multiplexer_3_out),
    .sel(tara_control_cs25b018_cs25b095_1_imm));
endmodule

module testing (
  input  in_1,
  input  in_2,
  input  [4:0] in_3,
  input  [3:0] in_4,
  output out_5,
  output out_6,
  output out_7,
  output out_8,
  output out_9,
  output out_10,
  output out_11,
  output out_12,
  output out_13,
  output out_14,
  output [1:0] out_15,
  output [4:0] out_16,
  output [2:0] out_17,
  output out_18,
  output out_19,
  output out_20,
  output out_21,
  output out_22
);

  tara_control_CS25B018_CS25B095 tara_control_cs25b018_cs25b095_1 (
    .Z(in_1), .N(in_2), .OPCODE(in_3), .TSTATE_OUT(in_4), .STEP_RST(out_5), .MAR_LOAD(out_6),
    .MDR_LOAD(out_7), .IR_LOAD(out_8), .ACC_LOAD(out_9), .REG_WE(out_10), .MEM_READ(out_11),
    .MEM_WRITE(out_12), .STATUS_WE(out_13), .IMM(out_14), .IMM_BIT_EXTEND(out_15), .ALU_OPCODE(out_16),
    .BUS_SOURCE(out_17), .PC_LOAD(out_18), .PC_FETCH_EN(out_19), .HALT(out_20), .SPARE_1(out_21),
    .SPARE_2(out_22));
endmodule
